// Logisim project main.circ as structural Verilog: 27 circuits, main circuit main
module main (
);

  wire button_1_out, button_3_out, clk, draw_module_1_drawing, draw_module_1_show, draw_module_1_write, shot;
  wire [3:0] bin_to_dec_1_output_1, bin_to_dec_1_output_2, bin_to_dec_2_output_1, bin_to_dec_2_output_2,
       bin_to_dec_3_output_1, bin_to_dec_3_output_2;
  wire [4:0] draw_module_1_line_num, game_1_x, game_1_y;
  wire [15:0] ai_score, game_1_command, game_1_id, hp, player_score, x_vec;
  wire [31:0] draw_module_1_line, video_buffer_32x32_1_out_5, video_buffer_32x32_1_out_6,
       video_buffer_32x32_1_out_7, video_buffer_32x32_1_out_8, video_buffer_32x32_1_out_9,
       video_buffer_32x32_1_out_10, video_buffer_32x32_1_out_11, video_buffer_32x32_1_out_12,
       video_buffer_32x32_1_out_13, video_buffer_32x32_1_out_14, video_buffer_32x32_1_out_15,
       video_buffer_32x32_1_out_16, video_buffer_32x32_1_out_17, video_buffer_32x32_1_out_18,
       video_buffer_32x32_1_out_19, video_buffer_32x32_1_out_20, video_buffer_32x32_1_out_21,
       video_buffer_32x32_1_out_22, video_buffer_32x32_1_out_23, video_buffer_32x32_1_out_24,
       video_buffer_32x32_1_out_25, video_buffer_32x32_1_out_26, video_buffer_32x32_1_out_27,
       video_buffer_32x32_1_out_28, video_buffer_32x32_1_out_29, video_buffer_32x32_1_out_30,
       video_buffer_32x32_1_out_31, video_buffer_32x32_1_out_32, video_buffer_32x32_1_out_33,
       video_buffer_32x32_1_out_34, video_buffer_32x32_1_out_35, video_buffer_32x32_1_out_36;

  Clock clock_1 (.out(clk));
  draw_module draw_module_1 (
    .clk(clk), .drawing(draw_module_1_drawing), .write(draw_module_1_write), .line(draw_module_1_line),
    .line_num(draw_module_1_line_num), .show(draw_module_1_show), .id(game_1_id), .x(game_1_x), .y(game_1_y),
    .command(game_1_command));
  game game_1 (
    .player_x_vec(x_vec), .ID(game_1_id), .X(game_1_x), .Y(game_1_y), .Command(game_1_command), .clock(clk),
    .drawing(draw_module_1_drawing), .player_score(player_score), .shot(shot), .hp(hp), .ai_score(ai_score));
  DotMatrix #(.inputtype("row"), .matrixcols(32), .matrixrows(32)) dotmatrix_1 (
    .row0(video_buffer_32x32_1_out_5), .row1(video_buffer_32x32_1_out_6), .row2(video_buffer_32x32_1_out_7),
    .row3(video_buffer_32x32_1_out_8), .row4(video_buffer_32x32_1_out_9), .row5(video_buffer_32x32_1_out_10),
    .row6(video_buffer_32x32_1_out_11), .row7(video_buffer_32x32_1_out_12),
    .row8(video_buffer_32x32_1_out_13), .row9(video_buffer_32x32_1_out_14),
    .row10(video_buffer_32x32_1_out_15), .row11(video_buffer_32x32_1_out_16),
    .row12(video_buffer_32x32_1_out_17), .row13(video_buffer_32x32_1_out_18),
    .row14(video_buffer_32x32_1_out_19), .row15(video_buffer_32x32_1_out_20),
    .row16(video_buffer_32x32_1_out_21), .row17(video_buffer_32x32_1_out_22),
    .row18(video_buffer_32x32_1_out_23), .row19(video_buffer_32x32_1_out_24),
    .row20(video_buffer_32x32_1_out_25), .row21(video_buffer_32x32_1_out_26),
    .row22(video_buffer_32x32_1_out_27), .row23(video_buffer_32x32_1_out_28),
    .row24(video_buffer_32x32_1_out_29), .row25(video_buffer_32x32_1_out_30),
    .row26(video_buffer_32x32_1_out_31), .row27(video_buffer_32x32_1_out_32),
    .row28(video_buffer_32x32_1_out_33), .row29(video_buffer_32x32_1_out_34),
    .row30(video_buffer_32x32_1_out_35), .row31(video_buffer_32x32_1_out_36));
  video_buffer_32x32 video_buffer_32x32_1 (
    .out_5(video_buffer_32x32_1_out_5), .out_6(video_buffer_32x32_1_out_6),
    .out_7(video_buffer_32x32_1_out_7), .out_8(video_buffer_32x32_1_out_8),
    .out_9(video_buffer_32x32_1_out_9), .out_10(video_buffer_32x32_1_out_10),
    .out_11(video_buffer_32x32_1_out_11), .out_12(video_buffer_32x32_1_out_12),
    .out_13(video_buffer_32x32_1_out_13), .out_14(video_buffer_32x32_1_out_14),
    .out_15(video_buffer_32x32_1_out_15), .out_16(video_buffer_32x32_1_out_16),
    .out_17(video_buffer_32x32_1_out_17), .out_18(video_buffer_32x32_1_out_18),
    .out_19(video_buffer_32x32_1_out_19), .out_20(video_buffer_32x32_1_out_20),
    .out_21(video_buffer_32x32_1_out_21), .out_22(video_buffer_32x32_1_out_22),
    .out_23(video_buffer_32x32_1_out_23), .out_24(video_buffer_32x32_1_out_24),
    .out_25(video_buffer_32x32_1_out_25), .out_26(video_buffer_32x32_1_out_26),
    .out_27(video_buffer_32x32_1_out_27), .out_28(video_buffer_32x32_1_out_28),
    .out_29(video_buffer_32x32_1_out_29), .out_30(video_buffer_32x32_1_out_30),
    .out_31(video_buffer_32x32_1_out_31), .out_32(video_buffer_32x32_1_out_32),
    .out_33(video_buffer_32x32_1_out_33), .out_34(video_buffer_32x32_1_out_34),
    .out_35(video_buffer_32x32_1_out_35), .out_36(video_buffer_32x32_1_out_36), .write(draw_module_1_write),
    .\input (draw_module_1_line), .y(draw_module_1_line_num), .show(draw_module_1_show));
  Button button_1 (.out(button_1_out));
  Button button_2 (.out(shot));
  Button button_3 (.out(button_3_out));
  controller controller_1 (.left(button_1_out), .right(button_3_out), .x_vec(x_vec));
  Hex_Digit_Display hex_digit_display_1 (.value(bin_to_dec_1_output_2));  // open: dp
  Hex_Digit_Display hex_digit_display_2 (.value(bin_to_dec_1_output_1));  // open: dp
  bin_to_dec bin_to_dec_1 (.input_hex(hp), .output_2(bin_to_dec_1_output_2), .output_1(bin_to_dec_1_output_1));
  Hex_Digit_Display hex_digit_display_3 (.value(bin_to_dec_2_output_1));  // open: dp
  Hex_Digit_Display hex_digit_display_4 (.value(bin_to_dec_2_output_2));  // open: dp
  bin_to_dec bin_to_dec_2 (
    .input_hex(player_score), .output_2(bin_to_dec_2_output_2), .output_1(bin_to_dec_2_output_1));
  Hex_Digit_Display hex_digit_display_5 (.value(bin_to_dec_3_output_1));  // open: dp
  Hex_Digit_Display hex_digit_display_6 (.value(bin_to_dec_3_output_2));  // open: dp
  bin_to_dec bin_to_dec_3 (.input_hex(ai_score), .output_2(bin_to_dec_3_output_2), .output_1(bin_to_dec_3_output_1));

  // Notes on the sheet:
  //   Shoot
  //   Movement
  //   <-
  //   ->
  //   HP
  //   PLAYER SCORE
  //   BOT SCORE
endmodule

module CDM16 (
  input  [15:0] adr,
  input  [15:0] val,
  input  clock,
  input  clock_2,
  input  write,
  input  write_2,
  input  hold,
  input  end_cycle,
  input  end_cycle_2,
  output drawing,
  output drawing_2,
  output [15:0] id,
  output [15:0] x,
  output [15:0] y,
  output [15:0] command,
  output \wait ,
  output run,
  output run_2,
  output button,
  output lose,
  output button_2,
  output [15:0] y_2,
  output [15:0] hp,
  output [15:0] player_score,
  output [15:0] ai_score
);

  wire and_2_out, and_3_out, and_4_out, and_5_out, and_6_out, and_7_out, and_8_out, and_10_out, and_11_out,
       and_12_out, and_13_out, and_15_out, and_16_out, and_17_out, and_18_out, bit_extender_1_out,
       cdm_16_1_p3, cdm_16_1_p4, code, comparator_3_eq, comparator_7_eq, comparator_8_eq, comparator_9_eq,
       comparator_10_eq, comparator_10_lt, comparator_12_eq, comparator_13_eq, comparator_15_eq, d_ff_1_q,
       d_ff_1_qn, data, decoder_1_out0, decoder_1_out1, initialized, mem, not_1_out, not_2_out, not_3_out,
       not_4_out, not_5_out, not_7_out, or_1_out, or_2_out, pull_resistor_6_node, pull_resistor_8_node,
       pull_resistor_10_node, pull_resistor_11_node, pull_resistor_12_node, pull_resistor_21_node,
       read_write, transistor_3_out, transistor_6_out, undriven, undriven_2, undriven_3, undriven_4, word,
       write_t;
  wire [15:0] cdm_16_1_p8, cdm_16_1_p9, cdm_16_1_p10, controlled_buffer_2_out, register_1_q, register_2_q,
       register_3_q, register_4_q, register_5_q, register_6_q, register_7_q, register_8_q, register_9_q,
       transistor_4_out;

  and and_1 (write_t, write, d_ff_1_q);
  not not_1 (not_1_out, clock);
  D_Flip_Flop d_ff_1 (
    .clk(not_1_out), .D(or_1_out), .Q(d_ff_1_q), .Qn(d_ff_1_qn), .preset(undriven), .en(undriven_2),
    .reset(undriven_3));
  D_Flip_Flop #(.trigger("falling")) d_ff_2 (
    .clk(not_1_out), .D(or_1_out), .Q(d_ff_1_q), .Qn(d_ff_1_qn), .preset(undriven), .en(undriven_2),
    .reset(undriven_3));
  or or_1 (or_1_out, write, and_2_out, or_2_out);
  or or_2 (or_2_out, hold, end_cycle);
  and and_2 (and_2_out, ~initialized, \wait );  // AND_Gate
  // CdM_16 cdm_16_1: pin names not known; wires that end beside it: d_ff_1_q, clock, cdm_16_1_p3, cdm_16_1_p4, mem, read_write, word, cdm_16_1_p8, cdm_16_1_p9, cdm_16_1_p10
  // Probe on cdm_16_1_p3
  // Probe on cdm_16_1_p3
  not not_2 (not_2_out, write_t);
  not not_3 (not_3_out, write_t);
  assign cdm_16_1_p10 = and_4_out ? controlled_buffer_2_out : 16'bz;  // Controlled_Buffer controlled_buffer_1
  assign controlled_buffer_2_out = and_3_out ? cdm_16_1_p9 : 16'bz;  // Controlled_Buffer controlled_buffer_2
  and and_3 (and_3_out, not_2_out, not_4_out);
  not not_4 (not_4_out, read_write);
  not not_5 (not_5_out, read_write);
  and and_4 (and_4_out, not_3_out, read_write);
  Transistor transistor_1 (.in(decoder_1_out0), .out(code), .gate(write_t));
  Pull_Resistor pull_resistor_1 (.node(code));
  Pull_Resistor #(.pull(1)) pull_resistor_2 (.node(data));
  Transistor #(.gate("br")) transistor_2 (.in(decoder_1_out1), .out(data), .gate(write_t));
  Decoder #(.disabled(0)) decoder_1 (.out0(decoder_1_out0), .out1(decoder_1_out1), .sel(cdm_16_1_p4), .en(mem));
  Decoder #(.disabled(0)) decoder_2 (.out0(decoder_1_out0), .out1(decoder_1_out1), .sel(cdm_16_1_p4), .en(mem));
  Transistor transistor_3 (.in(not_5_out), .out(transistor_3_out), .gate(write_t));
  Pull_Resistor #(.pull(1)) pull_resistor_3 (.node(transistor_3_out));
  Transistor #(.\type ("n"), .width(16)) transistor_4 (.in(adr), .out(transistor_4_out), .gate(write_t));
  Transistor #(.gate("br"), .width(16)) transistor_5 (.in(cdm_16_1_p8), .out(transistor_4_out), .gate(write_t));
  // Probe on transistor_4_out
  // Probe on transistor_4_out
  Transistor transistor_6 (.in(word), .out(transistor_6_out), .gate(undriven_4));
  Pull_Resistor #(.pull(1)) pull_resistor_4 (.node(transistor_6_out));
  Pull_Resistor #(.pull(1)) pull_resistor_5 (.node(transistor_6_out));
  Pull_Resistor pull_resistor_6 (.node(pull_resistor_6_node));
  Pull_Resistor pull_resistor_7 (.node(pull_resistor_6_node));
  Comparator #(.width(16)) comparator_1 (.a(transistor_4_out), .b(16'h86), .eq(pull_resistor_6_node));  // open: gt, lt
  Pull_Resistor pull_resistor_8 (.node(pull_resistor_8_node));
  Comparator #(.width(16)) comparator_2 (.a(transistor_4_out), .b(16'h88), .eq(pull_resistor_8_node));  // open: gt, lt
  Comparator #(.width(16)) comparator_3 (.a(transistor_4_out), .b(16'h8a), .eq(comparator_3_eq));  // open: gt, lt
  Pull_Resistor pull_resistor_9 (.node(comparator_3_eq));
  Pull_Resistor pull_resistor_10 (.node(pull_resistor_10_node));
  Comparator #(.width(16)) comparator_4 (.a(transistor_4_out), .b(16'h8c), .eq(pull_resistor_10_node));  // open: gt, lt
  Pull_Resistor pull_resistor_11 (.node(pull_resistor_11_node));
  Comparator #(.width(16)) comparator_5 (.a(transistor_4_out), .b(16'h84), .eq(pull_resistor_11_node));  // open: gt, lt
  Pull_Resistor pull_resistor_12 (.node(pull_resistor_12_node));
  Comparator #(.width(16)) comparator_6 (.a(transistor_4_out), .b(16'h96), .eq(pull_resistor_12_node));  // open: gt, lt
  Pull_Resistor pull_resistor_13 ();  // open: node
  Comparator #(.width(16)) comparator_7 (.a(transistor_4_out), .b(16'ha0), .eq(comparator_7_eq));  // open: gt, lt
  Pull_Resistor pull_resistor_14 (.node(comparator_7_eq));
  Pull_Resistor pull_resistor_15 ();  // open: node
  Comparator #(.width(16)) comparator_8 (.a(transistor_4_out), .b(16'h9c), .eq(comparator_8_eq));  // open: gt, lt
  Pull_Resistor pull_resistor_16 (.node(comparator_8_eq));
  Comparator #(.width(16)) comparator_9 (.a(transistor_4_out), .b(16'hae), .eq(comparator_9_eq));  // open: gt, lt
  Pull_Resistor pull_resistor_17 (.node(comparator_9_eq));
  Comparator #(.width(16)) comparator_10 (.eq(comparator_10_eq), .lt(comparator_10_lt));  // open: a, b, gt
  Comparator #(.width(16)) comparator_11 (
    .a(transistor_4_out), .b(16'hb0), .gt(comparator_10_eq), .eq(comparator_10_lt));  // open: lt
  Pull_Resistor pull_resistor_18 (.node(comparator_10_lt));
  Comparator #(.width(16)) comparator_12 (.a(transistor_4_out), .b(16'hc6), .eq(comparator_12_eq));  // open: gt, lt
  Pull_Resistor pull_resistor_19 (.node(comparator_12_eq));
  Comparator #(.width(16)) comparator_13 (.a(transistor_4_out), .b(16'hc8), .eq(comparator_13_eq));  // open: gt, lt
  Pull_Resistor pull_resistor_20 (.node(comparator_13_eq));
  Pull_Resistor pull_resistor_21 (.node(pull_resistor_21_node));
  Transistor #(.gate("br")) transistor_7 (.in(read_write), .out(pull_resistor_21_node), .gate(write_t));
  // ROM rom_1: pin names not known; wires that end beside it: transistor_4_out, code, word, controlled_buffer_2_out
  // RAM ram_1: pin names not known; wires that end beside it: transistor_4_out, transistor_6_out, data, clock, pull_resistor_21_node, controlled_buffer_2_out
  // RAM ram_2: pin names not known
  Register #(.width(16)) register_1 (.D(controlled_buffer_2_out), .Q(register_1_q), .clk(and_5_out));  // open: en, clr
  and and_5 (and_5_out, pull_resistor_6_node, data, transistor_3_out);
  Register #(.width(16)) register_2 (.D(controlled_buffer_2_out), .Q(register_2_q), .clk(and_6_out));  // open: en, clr
  and and_6 (and_6_out, pull_resistor_8_node, data, transistor_3_out);
  Register #(.width(16)) register_3 (.D(controlled_buffer_2_out), .Q(register_3_q), .clk(and_7_out));  // open: en, clr
  and and_7 (and_7_out, comparator_3_eq, data, transistor_3_out);
  Register #(.width(16)) register_4 (.D(controlled_buffer_2_out), .Q(register_4_q), .clk(and_8_out));  // open: en, clr
  and and_8 (and_8_out, pull_resistor_10_node, data, transistor_3_out);
  and and_9 (and_8_out, pull_resistor_10_node, data, transistor_3_out);
  Register #(.width(16)) register_5 (
    .D(controlled_buffer_2_out), .Q(register_5_q), .clk(and_10_out), .clr(end_cycle));  // open: en
  and and_10 (and_10_out, pull_resistor_11_node, data, transistor_3_out);
  Register #(.width(16)) register_6 (.D(controlled_buffer_2_out), .Q(register_6_q), .clk(and_11_out));  // open: en, clr
  and and_11 (and_11_out, pull_resistor_12_node, data, transistor_3_out);
  Register #(.width(16)) register_7 (.D(controlled_buffer_2_out), .Q(register_7_q), .clk(and_12_out));  // open: en, clr
  and and_12 (and_12_out, comparator_7_eq, data, transistor_3_out);
  Register #(.width(16)) register_8 (.D(controlled_buffer_2_out), .Q(register_8_q), .clk(and_13_out));  // open: en, clr
  and and_13 (and_13_out, comparator_8_eq, data, transistor_3_out);
  Register #(.width(16)) register_9 (.D(controlled_buffer_2_out), .Q(register_9_q), .clk(and_15_out));  // open: en, clr
  // AND_Gate and_14 is placed but not wired
  and and_15 (and_15_out, comparator_9_eq, data, transistor_3_out);
  Register #(.width(16)) register_10 (.en(controlled_buffer_2_out[0]));  // open: D, Q, clk, clr
  Register #(.width(16)) register_11 (.D(controlled_buffer_2_out), .Q(hp), .clk(and_16_out));  // open: en, clr
  and and_16 (and_16_out, comparator_10_lt, data, transistor_3_out);
  Register #(.width(16)) register_12 (
    .D(controlled_buffer_2_out), .Q(player_score), .clk(and_17_out));  // open: en, clr
  and and_17 (and_17_out, comparator_12_eq, data, transistor_3_out);
  Register #(.width(16)) register_13 (.D(controlled_buffer_2_out), .Q(ai_score), .clk(and_18_out));  // open: en, clr
  and and_18 (and_18_out, comparator_13_eq, data, transistor_3_out);
  Transistor #(.\type ("n"), .width(16)) transistor_8 (.in(val), .out(controlled_buffer_2_out), .gate(write_t));
  Transistor #(.\type ("n"), .width(16)) transistor_9 (.in(val), .out(controlled_buffer_2_out), .gate(write_t));
  assign id = drawing ? register_1_q : 16'bz;  // Controlled_Buffer controlled_buffer_3
  assign x = drawing ? register_2_q : 16'bz;  // Controlled_Buffer controlled_buffer_4
  assign y = drawing ? register_3_q : 16'bz;  // Controlled_Buffer controlled_buffer_5
  assign command = drawing ? register_4_q : 16'bz;  // Controlled_Buffer controlled_buffer_6
  Bit_Extender #(.in_width(16), .out_width(1)) bit_extender_1 (.in(register_6_q), .out(bit_extender_1_out));
  Bit_Extender #(.in_width(16), .out_width(1)) bit_extender_2 (.in(register_7_q), .out(button));
  Bit_Extender #(.in_width(16), .out_width(1)) bit_extender_3 (.in(register_8_q), .out(lose));
  Bit_Extender #(.in_width(16), .out_width(1)) bit_extender_4 ();  // open: in, out
  Bit_Extender #(.in_width(16), .out_width(1)) bit_extender_5 (.in(register_9_q), .out(y_2[0]));
  Comparator #(.width(16), .mode("unsigned")) comparator_14 (
    .a(register_5_q), .b(16'h2), .eq(drawing));  // open: gt, lt
  not not_6 (\wait , comparator_15_eq);
  Comparator #(.width(16), .mode("unsigned")) comparator_15 (
    .a(register_5_q), .b({16{1'b0}}), .eq(comparator_15_eq));  // open: gt, lt
  Comparator #(.width(16), .mode("unsigned")) comparator_16 ();  // open: a, b, gt, eq, lt
  not not_7 (not_7_out, drawing);
  xor xor_1 (run, not_7_out, bit_extender_1_out);
  Register #(.width(1)) u_initialized (.D(run), .Q(initialized), .clk(run));  // open: en, clr
  // Pins of 1 and 16 bits meet at controlled_buffer_2_out
  // Pins of 1 and 16 bits meet at y_2

  assign clock_2 = clock;
  assign drawing_2 = drawing;
  assign write_2 = write;

  // Other names for the same wires on the sheet: checker = \wait ; cl = clock; draw = drawing; end = end_cycle

  // Notes on the sheet:
  //   run
endmodule

module game (
  input  [15:0] player_x_vec,
  input  shot,
  input  clock,
  input  drawing,
  output [4:0] X,
  output [4:0] Y,
  output [15:0] ID,
  output [15:0] Command,
  output [15:0] hp,
  output [15:0] player_score,
  output [15:0] ai_score
);

  wire and_1_out, and_2_out, and_3_out, and_4_out, and_7_out, and_8_out, button, cdm16_1_drawing_2,
       collide_check_enemy, collide_check_player, collide_check_wall, command_draw, command_show,
       comparator_1_eq, comparator_6_eq, comparator_8_eq, comparator_9_eq, end_cycle,
       enemies_multiobject_1_initing_2, enemies_multiobject_1_ready, enemy_initing, hold, int_enemy,
       int_player, lose, not_1_out, or_4_out, or_5_out, player_initing, processor_draw, processor_drawing,
       pull_resistor_7_node, register_2_q, register_4_q, run, update_pl_pos, \wait , wait_int, write,
       xor_1_out;
  wire [5:0] enemies_multiobject_1_proc_command;
  wire [15:0] check2_writer_1_adr, check2_writer_1_val, collided, divider_1_out, divider_2_out,
       divider_3_out, divider_4_out, enemies_multiobject_1_x, enemies_multiobject_1_y, player_x_q,
       player_y_q, register_1_q, register_3_q, win, x_col, y_col;

  Comparator #(.width(16), .mode("unsigned")) comparator_1 (
    .a(player_x_vec), .b({16{1'b0}}), .eq(comparator_1_eq));  // open: gt, lt
  or or_1 (hold, enemy_initing, player_initing, processor_drawing);
  or or_2 (\wait , wait_int, write, drawing);
  or or_3 (end_cycle, win[0], lose);
  Pull_Resistor pull_resistor_1 (.node(collided));
  Register #(.width(16), .trigger("falling")) register_1 (
    .D(player_x_vec), .Q(register_1_q), .clk(xor_1_out));  // open: en, clr
  xor xor_1 (xor_1_out, comparator_1_eq, processor_draw);
  // Probe on enemies_multiobject_1_initing_2
  enemies_multiobject enemies_multiobject_1 (
    .\wait (\wait ), .draw(run), .id(ID), .y(enemies_multiobject_1_y), .x(enemies_multiobject_1_x),
    .command(Command), .ready(enemies_multiobject_1_ready), .initing(enemy_initing),
    .collide_check(collide_check_enemy), .clock(clock), .initing_2(enemies_multiobject_1_initing_2),
    .proc_command(enemies_multiobject_1_proc_command), .end_cycle(end_cycle), .x_col(x_col), .y_col(y_col),
    .collided(collided));
  Comparator #(.width(16), .mode("unsigned")) comparator_2 (.a(Command), .b(16'h1), .eq(command_draw));  // open: gt, lt
  Pull_Resistor pull_resistor_2 (.node(command_draw));
  Pull_Resistor pull_resistor_3 (.node(command_show));
  Comparator #(.width(16), .mode("unsigned")) comparator_3 (.a(Command), .b(16'h2), .eq(command_show));  // open: gt, lt
  Pull_Resistor pull_resistor_4 (.node(int_player));
  Comparator #(.width(6), .mode("unsigned")) comparator_4 (
    .a(enemies_multiobject_1_proc_command), .b({6{1'b0}}), .eq(int_player));  // open: gt, lt
  Pull_Resistor pull_resistor_5 (.node(int_enemy));
  Comparator #(.width(6), .mode("unsigned")) comparator_5 (
    .a(enemies_multiobject_1_proc_command), .b(6'b000001), .eq(int_enemy));  // open: gt, lt
  player_multiobject player_multiobject_1 (
    .draw(enemies_multiobject_1_ready), .id(ID), .x_2(enemies_multiobject_1_x), .y(enemies_multiobject_1_y),
    .x(register_1_q), .command(Command), .\wait (\wait ), .wait_2(clock), .end_cycle(end_cycle),
    .x_col(x_col), .y_col(y_col));
  // Probe on ID
  // Probe on enemies_multiobject_1_x
  // Probe on enemies_multiobject_1_y
  // Probe on Command
  Register #(.width(1)) register_2 (
    .D(processor_draw), .Q(register_2_q), .clk(processor_draw), .clr(and_1_out));  // open: en
  and and_1 (and_1_out, ~drawing, register_2_q);  // AND_Gate
  Divider #(.width(16)) divider_1 (.a(enemies_multiobject_1_x), .b(16'h2), .out(divider_1_out));  // open: upper, rem
  Bit_Extender #(.in_width(16), .out_width(5)) bit_extender_1 (.in(divider_1_out), .out(X));
  // Probe on X
  win_multiobject win_multiobject_1 (
    .\wait (\wait ), .draw(win[0]), .id(ID), .x(enemies_multiobject_1_x), .y(enemies_multiobject_1_y),
    .command(Command), .clock(clock));  // open: ready
  check2_writer check2_writer_1 (
    .adr(check2_writer_1_adr), .val(check2_writer_1_val), .write_3(write), .run(and_1_out), .clock_2(clock));
  // Probe on Y
  Bit_Extender #(.in_width(16), .out_width(5)) bit_extender_2 (.in(divider_2_out), .out(Y));
  Divider #(.width(16)) divider_2 (.a(enemies_multiobject_1_y), .b(16'h2), .out(divider_2_out));  // open: upper, rem
  Comparator #(.width(16), .mode("unsigned")) comparator_6 (
    .a(collided), .b({16{1'b0}}), .eq(comparator_6_eq));  // open: gt, lt
  not not_1 (not_1_out, comparator_6_eq);
  lose_multiobject lose_multiobject_1 (
    .\wait (\wait ), .draw(lose), .id(ID), .x(enemies_multiobject_1_x), .y(enemies_multiobject_1_y),
    .command(Command), .clock(clock));  // open: ready
  Register #(.width(16)) register_3 (.D(collided), .Q(register_3_q), .clk(not_1_out));  // open: en, clr
  collision_writer collision_writer_1 (
    .out_4(check2_writer_1_adr), .val(check2_writer_1_val), .write(write), .run(not_1_out), .clock(clock),
    .collided(register_3_q));
  enemy_writer enemy_writer_1 (
    .x(enemies_multiobject_1_x), .y(enemies_multiobject_1_y), .adr(check2_writer_1_adr),
    .val(check2_writer_1_val), .write(write), .clock(clock), .run(and_2_out));
  and and_2 (and_2_out, command_draw, int_enemy);
  Register #(.width(1)) register_4 (.D(and_3_out), .Q(register_4_q), .clk(and_3_out), .clr(and_4_out));  // open: en
  and and_3 (and_3_out, shot, ~button);  // AND_Gate
  and and_4 (and_4_out, register_4_q, ~write);  // AND_Gate
  and and_5 (update_pl_pos, int_player, command_draw);
  Register #(.width(16)) player_x (.D(enemies_multiobject_1_x), .Q(player_x_q), .clk(update_pl_pos));  // open: en, clr
  Register #(.width(16)) player_y (.D(enemies_multiobject_1_y), .Q(player_y_q), .clk(update_pl_pos));  // open: en, clr
  shoot_writer shoot_writer_1 (
    .adr(check2_writer_1_adr), .val(check2_writer_1_val), .run(and_4_out), .write(write), .clock(clock),
    .x(player_x_q), .y(player_y_q));
  Pull_Resistor pull_resistor_6 (.node(write));
  CDM16 cdm16_1 (
    .adr(check2_writer_1_adr), .val(check2_writer_1_val), .id(ID), .x(enemies_multiobject_1_x),
    .y(enemies_multiobject_1_y), .command(Command), .write_2(write), .hold(hold), .clock_2(clock),
    .\wait (wait_int), .run(run), .drawing_2(cdm16_1_drawing_2), .button(button), .lose(lose), .y_2(win),
    .hp(hp), .end_cycle(end_cycle), .player_score(player_score), .ai_score(ai_score));
  Divider #(.width(16)) divider_3 (.a(enemies_multiobject_1_x), .b(16'h2), .out(divider_3_out));  // open: upper, rem
  Register #(.width(16)) x_3 (.D(divider_3_out), .Q(x_col), .clk(or_5_out));  // open: en, clr
  Pull_Resistor pull_resistor_7 (.node(pull_resistor_7_node));
  Comparator #(.width(16), .mode("unsigned")) comparator_7 (
    .a(ID), .b(16'hf), .eq(pull_resistor_7_node));  // open: gt, lt
  Comparator #(.width(16), .mode("unsigned")) comparator_8 (.a(ID), .b(16'ha), .eq(comparator_8_eq));  // open: gt, lt
  Comparator #(.width(16), .mode("unsigned")) comparator_9 (.a(ID), .b(16'h14), .eq(comparator_9_eq));  // open: gt, lt
  Divider #(.width(16)) divider_4 (.a(enemies_multiobject_1_y), .b(16'h2), .out(divider_4_out));  // open: upper, rem
  Register #(.width(16)) y_3 (.D(divider_4_out), .Q(y_col), .clk(or_5_out));  // open: en, clr
  and and_6 (processor_drawing, cdm16_1_drawing_2, drawing);
  Pull_Resistor pull_resistor_8 (.node(comparator_8_eq));
  or or_4 (or_4_out, comparator_8_eq, comparator_9_eq);
  Pull_Resistor pull_resistor_9 (.node(comparator_9_eq));
  and and_7 (and_7_out, command_draw, pull_resistor_7_node);
  and and_8 (and_8_out, command_draw, or_4_out);
  or or_5 (or_5_out, and_8_out, and_7_out);
  D_Flip_Flop d_ff_1 (.clk(clock), .D(and_7_out), .Q(collide_check_player));  // open: Qn, preset, en, reset
  D_Flip_Flop d_ff_2 (.clk(clock), .D(and_8_out), .Q(collide_check_enemy));  // open: Qn, preset, en, reset
  D_Flip_Flop d_ff_3 (.clk(clock), .D(or_5_out), .Q(collide_check_wall));  // open: Qn, preset, en, reset
  // Pins of 1 and 16 bits meet at win

  // Other names for the same wires on the sheet: clk = clock
endmodule

module draw_module (
  input  clk,
  input  [15:0] command,
  input  [15:0] id,
  input  [4:0] x,
  input  [4:0] y,
  output drawing,
  output write,
  output [31:0] line,
  output show,
  output [4:0] line_num
);

  wire activator_q, and_1_out, comparator_1_eq, counter_1_carry, drawing_t, transistor_1_out;
  wire [4:0] counter_1_q, x_q, y_q;
  wire [15:0] adder_1_out, bit_extender_1_out, multiplier_1_out;
  wire [31:0] rom_1_data;

  simple_drawer_32x32 simple_drawer_32x32_1 (
    .x(x_q), .y(y_q), .texture_line(counter_1_q), .texture_input(rom_1_data), .cur_line(line_num),
    .line_x1(line));
  Counter #(.width(5), .max('h2)) counter_1 (
    .Q(counter_1_q), .carry(counter_1_carry), .clk(transistor_1_out), .clr(and_1_out));  // open: load, D, count
  Transistor #(.\type ("n"), .gate("br")) transistor_1 (.in(clk), .out(transistor_1_out), .gate(drawing_t));
  and and_1 (and_1_out, ~clk, counter_1_carry);  // AND_Gate
  D_Flip_Flop #(.trigger("falling")) synchronizer (
    .clk(clk), .D(activator_q), .Q(drawing_t), .reset(and_1_out));  // open: Qn, preset, en
  D_Flip_Flop activator (
    .clk(comparator_1_eq), .D(comparator_1_eq), .Q(activator_q), .reset(and_1_out));  // open: Qn, preset, en
  or or_1 (drawing, drawing_t, activator_q, and_1_out);
  assign bit_extender_1_out = {{11{1'b0}}, counter_1_q};  // Bit_Extender bit_extender_1
  Multiplier #(.width(16)) multiplier_1 (.a(id), .b(16'h3), .out(multiplier_1_out));  // open: cin, cout
  // Probe on id
  Adder #(.width(16)) adder_1 (.a(bit_extender_1_out), .b(multiplier_1_out), .out(adder_1_out));  // open: cin, cout
  Register #(.width(5)) u_y (.D(y), .Q(y_q), .clk(comparator_1_eq));  // open: en, clr
  Comparator #(.width(16), .mode("unsigned")) comparator_1 (
    .a(command), .b(16'h1), .eq(comparator_1_eq));  // open: gt, lt
  Pull_Resistor pull_resistor_1 (.node(comparator_1_eq));
  Comparator #(.width(16), .mode("unsigned")) comparator_2 (.a(command), .b(16'h2), .eq(show));  // open: gt, lt
  Pull_Resistor pull_resistor_2 (.node(show));
  Register #(.width(5)) u_x (.D(x), .Q(x_q), .clk(comparator_1_eq));  // open: en, clr
  and and_2 (write, drawing_t, ~clk);  // AND_Gate
  ROM #(.addrWidth(16), .dataWidth(32)) rom_1 (.addr(adder_1_out), .data(rom_1_data));  // open: sel

  // Other names for the same wires on the sheet: cmd_show = show

  // Notes on the sheet:
  //   texture line counter
  //   contents of rom_1 (hex, n*v repeats v):
  //   2 7 5 2 5 5 0 0 0 5 7 2 5 5 2 5 7 5 7 7 2 7 5 2 7 5 5 0 0 0 1 1 1 1151 1351 1551 1955 1155 114a
  //   7ce381 41441 3ce441 50441 51441 7ce39f 1 2 1 0 0 0 2 1 0 2 3 0 3 3 0 1 1 1
endmodule

module video_buffer_32x32 (
  input  write,
  input  [31:0] \input ,
  input  [4:0] y,
  input  show,
  output [31:0] out_5,
  output [31:0] out_6,
  output [31:0] out_7,
  output [31:0] out_8,
  output [31:0] out_9,
  output [31:0] out_10,
  output [31:0] out_11,
  output [31:0] out_12,
  output [31:0] out_13,
  output [31:0] out_14,
  output [31:0] out_15,
  output [31:0] out_16,
  output [31:0] out_17,
  output [31:0] out_18,
  output [31:0] out_19,
  output [31:0] out_20,
  output [31:0] out_21,
  output [31:0] out_22,
  output [31:0] out_23,
  output [31:0] out_24,
  output [31:0] out_25,
  output [31:0] out_26,
  output [31:0] out_27,
  output [31:0] out_28,
  output [31:0] out_29,
  output [31:0] out_30,
  output [31:0] out_31,
  output [31:0] out_32,
  output [31:0] out_33,
  output [31:0] out_34,
  output [31:0] out_35,
  output [31:0] out_36
);

  wire _0, _1, _2, _3, _4, _5, _6, _7, _8, _9, _10, _11, _12, _13, _14, _15, _16, _17, _18, _19, _20, _21,
       _22, _23, _24, _25, _26, _27, _28, _29, _30, _31;

  Decoder #(.select(5), .disabled(0)) decoder_1 (
    .out0(_0), .out1(_1), .out2(_2), .out3(_3), .out4(_4), .out5(_5), .out6(_6), .out7(_7), .out8(_8),
    .out9(_9), .out10(_10), .out11(_11), .out12(_12), .out13(_13), .out14(_14), .out15(_15), .out16(_16),
    .out17(_17), .out18(_18), .out19(_19), .out20(_20), .out21(_21), .out22(_22), .out23(_23), .out24(_24),
    .out25(_25), .out26(_26), .out27(_27), .out28(_28), .out29(_29), .out30(_30), .out31(_31), .sel(y),
    .en(write));
  // _32buffer_el 32buffer_el_1: pin names not known; wires that end beside it: \input , _0, out_5, show
  // _32buffer_el 32buffer_el_2: pin names not known; wires that end beside it: \input , _1, out_6, show
  // _32buffer_el 32buffer_el_3: pin names not known; wires that end beside it: \input , _2, out_7, show
  // _32buffer_el 32buffer_el_4: pin names not known; wires that end beside it: \input , _3, out_8, show
  // _32buffer_el 32buffer_el_5: pin names not known; wires that end beside it: \input , _4, out_9, show
  // _32buffer_el 32buffer_el_6: pin names not known; wires that end beside it: \input , _5, out_10, show
  // _32buffer_el 32buffer_el_7: pin names not known; wires that end beside it: \input , _6, out_11, show
  // _32buffer_el 32buffer_el_8: pin names not known; wires that end beside it: \input , _7, out_12, show
  // _32buffer_el 32buffer_el_9: pin names not known; wires that end beside it: \input , _8, out_13, show
  // _32buffer_el 32buffer_el_10: pin names not known; wires that end beside it: \input , _9, out_14, show
  // _32buffer_el 32buffer_el_11: pin names not known; wires that end beside it: \input , _10, out_15, show
  // _32buffer_el 32buffer_el_12: pin names not known; wires that end beside it: \input , _11, out_16, show
  // _32buffer_el 32buffer_el_13: pin names not known; wires that end beside it: \input , _12, out_17, show
  // _32buffer_el 32buffer_el_14: pin names not known; wires that end beside it: \input , _13, out_18, show
  // _32buffer_el 32buffer_el_15: pin names not known; wires that end beside it: \input , _14, out_19, show
  // _32buffer_el 32buffer_el_16: pin names not known; wires that end beside it: \input , _15, out_20, show
  // _32buffer_el 32buffer_el_17: pin names not known; wires that end beside it: \input , _16, out_21, show
  // _32buffer_el 32buffer_el_18: pin names not known; wires that end beside it: \input , _17, out_22, show
  // _32buffer_el 32buffer_el_19: pin names not known; wires that end beside it: \input , _18, out_23, show
  // _32buffer_el 32buffer_el_20: pin names not known; wires that end beside it: \input , _19, out_24, show
  // _32buffer_el 32buffer_el_21: pin names not known; wires that end beside it: \input , _20, out_25, show
  // _32buffer_el 32buffer_el_22: pin names not known; wires that end beside it: \input , _21, out_26, show
  // _32buffer_el 32buffer_el_23: pin names not known; wires that end beside it: \input , _22, out_27, show
  // _32buffer_el 32buffer_el_24: pin names not known; wires that end beside it: \input , _23, out_28, show
  // _32buffer_el 32buffer_el_25: pin names not known; wires that end beside it: \input , _24, out_29, show
  // _32buffer_el 32buffer_el_26: pin names not known; wires that end beside it: \input , _25, out_30, show
  // _32buffer_el 32buffer_el_27: pin names not known; wires that end beside it: \input , _26, out_31, show
  // _32buffer_el 32buffer_el_28: pin names not known; wires that end beside it: \input , _27, out_32, show
  // _32buffer_el 32buffer_el_29: pin names not known; wires that end beside it: \input , _28, out_33, show
  // _32buffer_el 32buffer_el_30: pin names not known; wires that end beside it: \input , _29, out_34, show
  // _32buffer_el 32buffer_el_31: pin names not known; wires that end beside it: \input , _30, out_35, show
  // _32buffer_el 32buffer_el_32: pin names not known; wires that end beside it: \input , _31, out_36, show

  // Other names for the same wires on the sheet: inp[31:0] = \input ; w = show

  // Notes on the sheet:
  //   write: pull=down
endmodule

module _32buffer_el (
  input  [31:0] \input ,
  input  [31:0] input_2,
  input  _1___buffer_read,
  input  _1___buffer_read_2,
  input  _1___buffer_write___clr,
  output [31:0] video,
  output [31:0] video_2
);

  wire [31:0] buffer_q, or_1_out;

  assign or_1_out = \input  | buffer_q;  // OR_Gate or_1, 32 bits wide
  assign or_1_out = \input  | buffer_q;  // OR_Gate or_2, 32 bits wide
  Register #(.width(32)) buffer (
    .D(or_1_out), .Q(buffer_q), .clk(_1___buffer_read), .clr(_1___buffer_write___clr));  // open: en
  Register #(.width(32)) u_video (.D(buffer_q), .Q(video), .clk(_1___buffer_write___clr));  // open: en, clr

  assign _1___buffer_read_2 = _1___buffer_read;
  assign input_2 = \input ;
  assign video_2 = video;
endmodule

module simple_drawer_32x32 (
  input  [4:0] texture_line,
  input  [31:0] texture_input,
  input  [4:0] x,
  input  [4:0] y,
  output [4:0] cur_line,
  output [31:0] line_x1
);

  wire [31:0] n32_bit_reverse_1_out_2;

  // Probe on x
  // Probe on y
  Adder #(.width(5)) adder_1 (.a(texture_line), .b(y), .out(cur_line));  // open: cin, cout
  _32_bit_reverse u_32_bit_reverse_1 (.in_1(texture_input), .out_2(n32_bit_reverse_1_out_2));
  Pull_Resistor pull_resistor_1 (.node(x));
  Shifter #(.width(32), .shift("lr")) shifter_1 (.in(n32_bit_reverse_1_out_2), .\dist (x), .out(line_x1));
endmodule

module _32_bit_reverse (
  input  [31:0] in_1,
  output [31:0] out_2
);


  assign out_2 = {in_1[0], in_1[1], in_1[2], in_1[3], in_1[4], in_1[5], in_1[6], in_1[7], in_1[8], in_1[9], in_1[10], in_1[11], in_1[12], in_1[13], in_1[14], in_1[15], in_1[16], in_1[17], in_1[18], in_1[19], in_1[20], in_1[21], in_1[22], in_1[23], in_1[24], in_1[25], in_1[26], in_1[27], in_1[28], in_1[29], in_1[30], in_1[31]};
endmodule

module player_multiobject (
  input  collide_check,
  input  [15:0] x,
  input  \wait ,
  input  [15:0] x_col,
  input  end_cycle,
  input  draw,
  input  wait_2,
  input  [15:0] y_col,
  output [15:0] collided,
  output initing,
  output [15:0] id,
  output [15:0] x_2,
  output [15:0] y,
  output [15:0] command,
  output [5:0] proc_command,
  output ready
);

  wire adder_1_p2, adder_1_p4, and_1_out, and_2_out, and_3_out, collided_t, comparator_1_eq, comparator_2_lt,
       comparator_3_eq, comparator_3_gt, comparator_4_gt, counter_1_p2, d_ff_1_q, draw_t, init_step,
       initing_t, not_1_out, not_4_out, not_5_out, not_6_out, not_7_out, not_8_out, or_1_out, or_2_out,
       register_1_q, register_2_q, transistor_1_out, undriven, undriven_3;
  wire [2:0] undriven_2;
  wire [15:0] adder_1_p1, adder_1_p3, controlled_buffer_1_out, divider_1_out, divider_2_out,
       multiplexer_3_out, subtractor_1_out, subtractor_2_out, x_t;

  Bit_Extender #(.in_width(2), .out_width(1)) bit_extender_1 (.out(init_step));  // open: in
  // Counter #(.width(2), .max('h2)) counter_1: pin names not known; wires that end beside it: wait_2, counter_1_p2, counter_1_p2
  or or_1 (or_1_out, end_cycle, ready);
  Register #(.width(1)) register_1 (.D(undriven), .Q(register_1_q));  // open: en, clk, clr
  not not_1 (not_1_out, \wait );
  Register #(.width(1)) register_2 (.D(draw), .Q(register_2_q), .clk(draw), .clr(or_1_out));  // open: en
  // NOT_Gate not_2 is placed but not wired
  Counter #(.width(3), .max('h2)) counter_2 (
    .carry(ready), .clk(transistor_1_out), .clr(ready));  // open: load, D, count, Q
  Transistor #(.\type ("n")) transistor_1 (.in(wait_2), .out(transistor_1_out), .gate(and_1_out));
  and and_1 (and_1_out, not_1_out, register_2_q);
  Multiplexer #(.enable("false")) multiplexer_1 (.in0(register_2_q), .in1(init_step), .out(draw_t), .sel(initing_t));
  // NOT_Gate not_3 has open pins: in=undriven_3, out=open
  // Adder #(.width(16)) adder_1: pin names not known; wires that end beside it: adder_1_p1, adder_1_p2, adder_1_p3, adder_1_p4
  Multiplexer #(.width(16), .enable("false")) multiplexer_2 (
    .in1(16'ha), .out(adder_1_p1), .sel(initing_t));  // open: in0
  Comparator #(.width(3), .mode("unsigned")) comparator_1 (
    .a(undriven_2), .b(3'b001), .eq(comparator_1_eq));  // open: gt, lt
  Transistor #(.\type ("n"), .width(16)) transistor_2 (.in(16'h1), .gate(d_ff_1_q));  // open: out
  D_Flip_Flop #(.trigger("falling")) d_ff_1 (
    .clk(wait_2), .D(undriven_3), .Q(d_ff_1_q), .Qn(d_ff_1_q));  // open: preset, en, reset
  Register #(.width(16)) u_x (.D(adder_1_p3), .clk(draw_t));  // open: en, Q, clr
  Multiplexer #(.width(16), .enable("false")) multiplexer_3 (
    .in0({16{1'b0}}), .in1(16'h1), .out(multiplexer_3_out));  // open: sel
  assign controlled_buffer_1_out = draw_t ? {16{1'b0}} : 16'bz;  // Controlled_Buffer controlled_buffer_1
  not not_4 (not_4_out, initing_t);
  Controlled_Buffer #(.width(16)) controlled_buffer_2 (.en(draw_t));  // open: in, out
  not not_5 (not_5_out, initing_t);
  Controlled_Buffer #(.width(16)) controlled_buffer_3 (.en(draw_t));  // open: in, out
  not not_6 (not_6_out, initing_t);
  Controlled_Buffer #(.width(16)) controlled_buffer_4 (.in(multiplexer_3_out), .en(draw_t));  // open: out
  not not_7 (not_7_out, initing_t);
  Controlled_Buffer #(.width(6)) controlled_buffer_5 (.in({6{1'b0}}), .en(draw_t));  // open: out
  not not_8 (not_8_out, initing_t);
  assign id = not_4_out ? controlled_buffer_1_out : 16'bz;  // Controlled_Buffer controlled_buffer_6
  Controlled_Buffer #(.width(16)) controlled_buffer_7 (.en(not_5_out));  // open: in, out
  Controlled_Buffer #(.width(16)) controlled_buffer_8 (.out(y), .en(not_6_out));  // open: in
  Controlled_Buffer #(.width(16)) controlled_buffer_9 (.out(command), .en(not_7_out));  // open: in
  Controlled_Buffer #(.width(6)) controlled_buffer_10 (.out(proc_command), .en(not_8_out));  // open: in
  Pull_Resistor pull_resistor_1 (.node(x_col));
  Pull_Resistor pull_resistor_2 (.node(y_col));
  // Probe on x_col
  Divider #(.width(16)) divider_1 (.a(x_t), .b(16'h2), .out(divider_1_out));  // open: upper, rem
  // Probe on y_col
  Divider #(.width(16)) divider_2 (.a(16'h38), .b(16'h2), .out(divider_2_out));  // open: upper, rem
  Subtractor #(.width(16)) subtractor_1 (.a(x_col), .b(divider_1_out), .out(subtractor_1_out));  // open: bin, bout
  // Probe on subtractor_2_out
  Subtractor #(.width(16)) subtractor_2 (.a(y_col), .b(divider_2_out), .out(subtractor_2_out));  // open: bin, bout
  // Probe on 16'hfffd
  Comparator #(.width(16)) comparator_2 (.a(subtractor_1_out), .b(16'h3), .lt(comparator_2_lt));  // open: gt, eq
  Comparator #(.width(16)) comparator_3 (
    .a(subtractor_1_out), .b({16{1'b0}}), .gt(comparator_3_gt), .eq(comparator_3_eq));  // open: lt
  Comparator #(.width(16)) comparator_4 (.a(subtractor_2_out), .b(16'hfffd), .gt(comparator_4_gt));  // open: eq, lt
  and and_2 (and_2_out, comparator_2_lt, or_2_out);
  or or_2 (or_2_out, comparator_3_gt, comparator_3_eq);
  and and_3 (and_3_out, and_2_out, comparator_4_gt);
  and and_4 (collided_t, and_3_out, collide_check);

  // Other names for the same wires on the sheet: clk = wait_2
endmodule

module enemies_multiobject (
  input  collide_check,
  input  \wait ,
  input  end_cycle,
  input  draw,
  input  [15:0] x_col,
  input  clock,
  input  [15:0] y_col,
  output [15:0] collided,
  output [15:0] id,
  output initing,
  output [15:0] y,
  output initing_2,
  output [15:0] x,
  output [15:0] command,
  output [5:0] proc_command,
  output ready
);

  wire alive, and_1_out, and_2_out, and_4_out, and_5_out, and_7_out, and_8_out, and_9_out, and_10_out,
       and_11_out, and_12_out, and_13_out, collided_t, comparator_1_eq, comparator_1_gt, comparator_2_eq,
       comparator_2_lt, comparator_4_lt, comparator_5_eq, comparator_5_lt, comparator_6_eq, comparator_6_lt,
       comparator_8_eq, comparator_8_lt, counter_1_carry, draw_t, may_collide, multiplexer_2_out, not_1_out,
       not_2_out, not_3_out, not_5_out, not_6_out, not_7_out, or_1_out, or_2_out, or_4_out, or_5_out,
       or_6_out, or_7_out, or_8_out, or_9_out, or_10_out, or_11_out, or_12_out, pull_resistor_1_node,
       pull_resistor_2_node, pull_resistor_3_node, register_1_q, register_2_q, register_4_q, register_5_q,
       register_9_q, register_10_q, texture_state, wait_t, x_aligned, xnor_1_out;
  wire [4:0] col_adr, counter_1_q;
  wire [4:1] multiplexer_1_out;
  wire [15:0] adder_1_out, adder_2_out, adder_3_out, adder_4_out, adder_5_out, adder_6_out, adder_7_out,
       adder_8_out, bit_extender_1_out, controlled_buffer_4_out, divider_1_out, divider_1_rem, divider_2_out,
       divider_3_out, divider_4_out, divider_4_rem, divider_5_out, divider_5_rem, multiplexer_3_out,
       multiplexer_4_out, multiplexer_5_out, multiplexer_6_out, multiplier_1_out, multiplier_2_out,
       multiplier_3_out, multiplier_4_out, multiplier_5_out, negator_1_out, negator_2_out, register_6_p1,
       register_11_q, register_12_q, subtractor_2_out, subtractor_3_out, x_t, y_t;

  not not_1 (not_1_out, may_collide);
  and and_1 (and_1_out, collided_t, alive);
  D_Flip_Flop #(.trigger("falling")) d_ff_1 (
    .clk(clock), .D(may_collide), .Q(collided_t), .reset(not_1_out));  // open: Qn, preset, en
  Register #(.width(1)) register_1 (.D(or_1_out), .Q(register_1_q), .clk(clock));  // open: en, clr
  or or_1 (or_1_out, collide_check, \wait );
  Register #(.width(1)) register_2 (.D(draw), .Q(register_2_q), .clk(draw), .clr(or_2_out));  // open: en
  or or_2 (or_2_out, end_cycle, ready);
  Transistor #(.\type ("n")) transistor_1 (.in(1'b0), .out(collided[0]), .gate(and_1_out));
  or or_3 (wait_t, register_1_q, or_1_out);
  Register #(.width(1)) register_3 (.D(register_2_q), .Q(draw_t), .clk(and_2_out), .clr(or_2_out));  // open: en
  and and_2 (and_2_out, clock, ~wait_t);  // AND_Gate
  // AND_Gate and_3 is placed but not wired
  Counter #(.width(5), .max('he)) counter_1 (
    .Q(counter_1_q), .carry(counter_1_carry), .clk(not_3_out));  // open: load, D, count, clr
  Multiplexer #(.width(5), .enable("false")) multiplexer_1 (
    .in0(counter_1_q), .in1(col_adr), .out({multiplexer_1_out, initing_2}), .sel(may_collide));
  not not_2 (not_2_out, counter_1_carry);
  not not_3 (not_3_out, multiplexer_2_out);
  Multiplexer #(.enable("false")) multiplexer_2 (
    .in0(clock), .in1(pull_resistor_1_node), .out(multiplexer_2_out), .sel(register_4_q));
  Pull_Resistor pull_resistor_1 (.node(pull_resistor_1_node));
  Transistor #(.\type ("n"), .gate("br")) transistor_2 (.in(or_4_out), .out(pull_resistor_1_node), .gate(draw_t));
  or or_4 (or_4_out, wait_t, and_4_out);
  and and_4 (and_4_out, ~clock, ~and_5_out);  // AND_Gate
  not not_4 (initing, register_4_q);
  Register #(.width(1)) register_4 (.D(not_2_out), .Q(register_4_q), .clk(not_2_out));  // open: en, clr
  Negator #(.width(16)) negator_1 (.in(16'h1), .out(negator_1_out));
  assign bit_extender_1_out = {{11{1'b0}}, {multiplexer_1_out, initing_2}};  // Bit_Extender bit_extender_1
  Pull_Resistor pull_resistor_2 (.node(pull_resistor_2_node));
  Transistor #(.gate("br")) transistor_3 (.in(1'b1), .out(pull_resistor_2_node), .gate(register_4_q));
  xnor xnor_1 (xnor_1_out, collided_t, register_4_q);
  Register #(.width(1)) register_5 (.D(not_2_out), .Q(register_5_q), .clk(not_2_out), .clr(register_5_q));  // open: en
  Multiplexer #(.width(16), .enable("false")) multiplexer_3 (
    .in0(16'h1), .in1(negator_1_out), .out(multiplexer_3_out), .sel(register_9_q));
  RAM #(.addrWidth(5), .dataWidth(1), .bus("separate")) ram_1 (
    .addr({multiplexer_1_out, initing_2}), .din(pull_resistor_2_node), .data(alive), .str(xnor_1_out),
    .clk(clock));  // open: sel, ld, clr
  // Register #(.width(16)) register_6: pin names not known; wires that end beside it: register_6_p1
  // Probe on register_6_p1
  Adder #(.width(16)) adder_1 (.a(x_t), .b(multiplexer_3_out), .out(adder_1_out));  // open: cin, cout
  Adder #(.width(16)) adder_2 (.a(16'h2), .b(y_t), .out(adder_2_out));  // open: cin, cout
  and and_5 (and_5_out, alive, register_4_q);
  and and_6 (ready, register_5_q, draw_t);
  Register #(.width(16)) register_7 (.D(adder_1_out), .Q(x_t), .clk(draw_t));  // open: en, clr
  Register #(.width(16)) register_8 (.D(adder_2_out), .Q(y_t), .clk(and_7_out));  // open: en, clr
  and and_7 (and_7_out, register_10_q, ready);
  Divider #(.width(16)) divider_1 (
    .a(bit_extender_1_out), .b(16'h5), .out(divider_1_out), .rem(divider_1_rem));  // open: upper
  Counter #(.width(1), .max('h1)) counter_2 (
    .Q(texture_state), .clk(register_5_q));  // open: load, D, count, carry, clr
  // Probe on negator_2_out
  or or_5 (or_5_out, comparator_1_gt, comparator_1_eq);
  Comparator #(.width(16), .mode("unsigned")) comparator_1 (
    .a(x_t), .b(register_6_p1), .gt(comparator_1_gt), .eq(comparator_1_eq));  // open: lt
  Multiplier #(.width(16)) multiplier_1 (.a(divider_1_out), .b(16'ha), .out(multiplier_1_out));  // open: cin, cout
  Multiplier #(.width(16)) multiplier_2 (.a(divider_1_rem), .b(16'ha), .out(multiplier_2_out));  // open: cin, cout
  Multiplexer #(.width(16), .enable("false")) multiplexer_4 (
    .in0({16{1'b0}}), .in1(16'h1), .out(multiplexer_4_out), .sel(and_8_out));
  and and_8 (and_8_out, and_5_out, or_6_out);
  or or_6 (or_6_out, not_5_out, wait_t);
  not not_5 (not_5_out, clock);
  Comparator #(.width(16)) comparator_2 (
    .a(x_t), .b(negator_2_out), .eq(comparator_2_eq), .lt(comparator_2_lt));  // open: gt
  Adder #(.width(16)) adder_3 (.a(16'h3), .b(divider_1_out), .out(adder_3_out));  // open: cin, cout
  Adder #(.width(16)) adder_4 (.a(16'h6), .b(divider_1_out), .out(adder_4_out));  // open: cin, cout
  Adder #(.width(16)) adder_5 (.a(y_t), .b(multiplier_1_out), .out(adder_5_out));  // open: cin, cout
  Adder #(.width(16)) adder_6 (.a(x_t), .b(multiplier_2_out), .out(adder_6_out));  // open: cin, cout
  or or_7 (or_7_out, comparator_2_eq, comparator_2_lt);
  Register #(.width(1)) register_9 (.D(or_5_out), .Q(register_9_q), .clk(or_5_out), .clr(and_9_out));  // open: en
  Register #(.width(1)) register_10 (.D(or_8_out), .Q(register_10_q), .clk(or_8_out), .clr(and_7_out));  // open: en
  or or_8 (or_8_out, or_5_out, and_9_out);
  Multiplexer #(.width(16), .enable("false")) multiplexer_5 (
    .in0(adder_3_out), .in1(adder_4_out), .out(multiplexer_5_out), .sel(texture_state));
  assign id = draw_t ? multiplexer_5_out : 16'bz;  // Controlled_Buffer controlled_buffer_1
  assign y = draw_t ? adder_5_out : 16'bz;  // Controlled_Buffer controlled_buffer_2
  assign x = draw_t ? adder_6_out : 16'bz;  // Controlled_Buffer controlled_buffer_3
  assign controlled_buffer_4_out = alive ? divider_1_rem : 16'bz;  // Controlled_Buffer controlled_buffer_4
  assign command = draw_t ? multiplexer_4_out : 16'bz;  // Controlled_Buffer controlled_buffer_5
  assign proc_command = draw_t ? 6'b000001 : 6'bz;  // Controlled_Buffer controlled_buffer_6
  and and_9 (and_9_out, or_7_out, register_9_q);
  and and_10 (and_10_out, pull_resistor_3_node, wait_t);
  Pull_Resistor pull_resistor_3 (.node(pull_resistor_3_node));
  Comparator #(.width(16), .mode("unsigned")) comparator_3 (
    .a(controlled_buffer_4_out), .b(register_12_q), .gt(pull_resistor_3_node));  // open: eq, lt
  Multiplexer #(.width(16), .enable("false")) multiplexer_6 (
    .in0(16'h30), .in1(controlled_buffer_4_out), .out(multiplexer_6_out), .sel(draw_t));
  Register #(.width(16)) register_11 (.D(multiplexer_6_out), .Q(register_11_q), .clk(or_9_out));  // open: en, clr
  or or_9 (or_9_out, and_11_out, and_12_out);
  and and_11 (and_11_out, comparator_4_lt, wait_t);
  Comparator #(.width(16), .mode("unsigned")) comparator_4 (
    .a(controlled_buffer_4_out), .b(register_11_q), .lt(comparator_4_lt));  // open: gt, eq
  Pull_Resistor pull_resistor_4 (.node(comparator_4_lt));
  Register #(.width(16)) register_12 (
    .D(controlled_buffer_4_out), .Q(register_12_q), .clk(and_10_out), .clr(not_6_out));  // open: en
  not not_6 (not_6_out, draw_t);
  Pull_Resistor pull_resistor_5 (.node(x_col));
  Pull_Resistor pull_resistor_6 (.node(y_col));
  Multiplier #(.width(16)) multiplier_3 (.a(16'h8), .b(adder_7_out), .out(multiplier_3_out));  // open: cin, cout
  Adder #(.width(16)) adder_7 (.a(16'h1), .b(register_12_q), .out(adder_7_out));  // open: cin, cout
  // Probe on x_col
  Divider #(.width(16)) divider_2 (.a(x_t), .b(16'h2), .out(divider_2_out));  // open: upper, rem
  // Probe on divider_2_out
  Divider #(.width(16)) divider_3 (.a(y_t), .b(16'h2), .out(divider_3_out));  // open: upper, rem
  not not_7 (not_7_out, draw_t);
  and and_12 (and_12_out, not_7_out, clock);
  Multiplier #(.width(16)) multiplier_4 (.a(register_11_q), .b(16'ha), .out(multiplier_4_out));  // open: cin, cout
  Negator #(.width(16)) negator_2 (.in(multiplier_4_out), .out(negator_2_out));
  Subtractor #(.width(16)) subtractor_1 (.a(16'h3b), .b(multiplier_3_out), .out(register_6_p1));  // open: bin, bout
  // Probe on subtractor_2_out
  Subtractor #(.width(16)) subtractor_2 (.a(x_col), .b(divider_2_out), .out(subtractor_2_out));  // open: bin, bout
  // Probe on divider_4_rem
  Subtractor #(.width(16)) subtractor_3 (.a(y_col), .b(divider_3_out), .out(subtractor_3_out));  // open: bin, bout
  Divider #(.width(16)) divider_4 (
    .a(subtractor_2_out), .b(16'h5), .out(divider_4_out), .rem(divider_4_rem));  // open: upper
  Comparator #(.width(16), .mode("unsigned")) comparator_5 (
    .a(divider_4_rem), .b(16'h2), .eq(comparator_5_eq), .lt(comparator_5_lt));  // open: gt
  Divider #(.width(16)) divider_5 (
    .a(subtractor_3_out), .b(16'h5), .out(divider_5_out), .rem(divider_5_rem));  // open: upper
  Comparator #(.width(16), .mode("unsigned")) comparator_6 (
    .a(divider_5_rem), .b(16'h2), .eq(comparator_6_eq), .lt(comparator_6_lt));  // open: gt
  Comparator #(.width(16), .mode("unsigned")) comparator_7 (
    .a(divider_4_out), .b(16'h6), .lt(x_aligned));  // open: gt, eq
  // Probe on divider_4_out
  or or_10 (or_10_out, comparator_5_eq, comparator_5_lt);
  and and_13 (and_13_out, or_10_out, or_11_out);
  Multiplier #(.width(16)) multiplier_5 (.a(divider_5_out), .b(16'h5), .out(multiplier_5_out));  // open: cin, cout
  // Probe on multiplier_5_out
  or or_11 (or_11_out, comparator_6_eq, comparator_6_lt);
  // Probe on adder_8_out
  Adder #(.width(16)) adder_8 (.a(divider_4_out), .b(multiplier_5_out), .out(adder_8_out));  // open: cin, cout
  Comparator #(.width(16), .mode("unsigned")) comparator_8 (
    .a(adder_8_out), .b(16'he), .eq(comparator_8_eq), .lt(comparator_8_lt));  // open: gt
  Bit_Extender #(.in_width(16), .out_width(5)) bit_extender_2 (.in(adder_8_out), .out(col_adr));
  or or_12 (or_12_out, comparator_8_eq, comparator_8_lt);
  and and_14 (may_collide, or_12_out, and_13_out, collide_check, x_aligned);
  // Pins of 1 and 16 bits meet at collided
  // Pins of 1 and 16 bits meet at 16'h2
  // Pins of 1 and 5 bits meet at {multiplexer_1_out, initing_2}

  // Other names for the same wires on the sheet: clk = clock

  // Notes on the sheet:
  //   enemy matrix
  //   enemies in row
  //   rows delta
  //   columns delta
  //   base texture id1
  //   base texture id2
  //   output X
  //   output Y
endmodule

module win_multiobject (
  input  \wait ,
  input  draw,
  input  clock,
  output [15:0] id,
  output [15:0] x,
  output [15:0] y,
  output [15:0] command,
  output ready
);

  wire and_1_out, comparator_1_eq, draw_t, not_1_out, not_2_out, register_1_q, transistor_1_out, undriven;
  wire [3:0] counter_1_q;
  wire [15:0] bit_extender_1_out, multiplexer_1_out, multiplexer_2_out, multiplexer_3_out, multiplexer_4_out;

  Register #(.width(1)) register_1 (.D(draw), .Q(register_1_q), .clk(draw), .clr(ready));  // open: en
  Register #(.width(1)) register_2 (.D(register_1_q), .Q(draw_t), .clk(not_1_out), .clr(ready));  // open: en
  not not_1 (not_1_out, clock);
  not not_2 (not_2_out, \wait );
  Counter #(.width(4), .max('h5)) counter_1 (
    .Q(counter_1_q), .carry(ready), .clk(transistor_1_out), .clr(ready));  // open: load, D, count
  Transistor #(.\type ("n"), .fanout(1), .incoming(4), .appear("center"), .bit0("none"), .bit1(0), .bit2("none"), .bit3("none")) transistor_1 (
    .in(clock), .out(transistor_1_out), .gate(and_1_out));
  Transistor #(.\type ("n")) transistor_2 (.in(clock), .out(transistor_1_out), .gate(and_1_out));
  and and_1 (and_1_out, not_2_out, draw_t);
  Multiplexer #(.width(16), .enable("false")) multiplexer_1 (
    .in0(16'hb), .in1(16'hc), .out(multiplexer_1_out), .sel(undriven));
  Multiplexer #(.width(16), .enable("false")) multiplexer_2 (
    .in0(16'h1a), .in1(16'h20), .out(multiplexer_2_out), .sel(undriven));
  Comparator #(.width(4), .mode("unsigned")) comparator_1 (
    .a(counter_1_q), .b(4'b0000), .eq(comparator_1_eq));  // open: gt, lt
  assign bit_extender_1_out = {{15{1'b0}}, counter_1_q[0]};  // Bit_Extender bit_extender_1
  assign id = draw_t ? multiplexer_1_out : 16'bz;  // Controlled_Buffer controlled_buffer_1
  assign x = draw_t ? 16'h10 : 16'bz;  // Controlled_Buffer controlled_buffer_2
  assign y = draw_t ? multiplexer_2_out : 16'bz;  // Controlled_Buffer controlled_buffer_3
  Multiplexer #(.width(16), .enable("false")) multiplexer_3 (
    .in0(multiplexer_4_out), .in1(16'h2), .out(multiplexer_3_out), .sel(comparator_1_eq));
  Multiplexer #(.width(16), .enable("false")) multiplexer_4 (
    .in0(bit_extender_1_out), .in1(16'h2), .out(multiplexer_4_out), .sel(counter_1_q[2]));
  assign command = draw_t ? multiplexer_3_out : 16'bz;  // Controlled_Buffer controlled_buffer_4

  // Other names for the same wires on the sheet: clk = clock
endmodule

module lose_multiobject (
  input  \wait ,
  input  draw,
  input  clock,
  output [15:0] id,
  output [15:0] x,
  output [15:0] y,
  output [15:0] command,
  output ready
);

  wire and_1_out, comparator_1_eq, draw_t, not_1_out, not_2_out, register_2_q, transistor_1_out;
  wire [3:0] counter_1_q;
  wire [15:0] bit_extender_1_out, multiplexer_1_out, multiplexer_2_out, multiplexer_3_out, multiplexer_4_out;

  Register #(.width(1)) register_1 (.D(register_2_q), .Q(draw_t), .clk(not_1_out), .clr(ready));  // open: en
  Register #(.width(1)) register_2 (.D(draw), .Q(register_2_q), .clk(draw), .clr(ready));  // open: en
  not not_1 (not_1_out, clock);
  not not_2 (not_2_out, \wait );
  Counter #(.width(4), .max('hf)) counter_1 (
    .Q(counter_1_q), .carry(ready), .clk(transistor_1_out), .clr(ready));  // open: load, D, count
  Transistor #(.\type ("n")) transistor_1 (.in(clock), .out(transistor_1_out), .gate(and_1_out));
  and and_1 (and_1_out, not_2_out, draw_t);
  Multiplexer #(.width(16), .enable("false")) multiplexer_1 (
    .in0(16'hd), .in1(16'he), .out(multiplexer_1_out), .sel(counter_1_q[1]));
  Multiplexer #(.width(16), .enable("false")) multiplexer_2 (
    .in0(16'h1a), .in1(16'h20), .out(multiplexer_2_out), .sel(counter_1_q[1]));
  Comparator #(.width(4), .mode("unsigned")) comparator_1 (
    .a(counter_1_q), .b(4'b0000), .eq(comparator_1_eq));  // open: gt, lt
  assign bit_extender_1_out = {{15{1'b0}}, counter_1_q[0]};  // Bit_Extender bit_extender_1
  assign id = draw_t ? multiplexer_1_out : 16'bz;  // Controlled_Buffer controlled_buffer_1
  assign x = draw_t ? 16'h8 : 16'bz;  // Controlled_Buffer controlled_buffer_2
  assign y = draw_t ? multiplexer_2_out : 16'bz;  // Controlled_Buffer controlled_buffer_3
  Multiplexer #(.width(16), .enable("false")) multiplexer_3 (
    .in0(bit_extender_1_out), .in1(16'h2), .out(multiplexer_3_out), .sel(counter_1_q[2]));
  Multiplexer #(.width(16), .enable("false")) multiplexer_4 (
    .in0(multiplexer_3_out), .in1(16'h2), .out(multiplexer_4_out), .sel(comparator_1_eq));
  assign command = draw_t ? multiplexer_4_out : 16'bz;  // Controlled_Buffer controlled_buffer_4

  // Other names for the same wires on the sheet: clk = clock
endmodule

module enemy_writer (
  input  [15:0] y,
  input  [15:0] x,
  input  run,
  input  clock,
  output [15:0] val,
  output [15:0] adr,
  output write
);

  wire activate_q, controlled_buffer_1_out, counter_1_carry, not_1_out, not_2_out, writing;
  wire [2:0] counter_1_q, random_1_out;
  wire [15:0] bit_extender_1_out, multiplexer_1_out, multiplexer_2_out;

  assign controlled_buffer_1_out = writing ? clock : 1'bz;  // Controlled_Buffer controlled_buffer_1
  Pull_Resistor pull_resistor_1 (.node(controlled_buffer_1_out));
  Random #(.width(3)) random_1 (.clk(controlled_buffer_1_out), .out(random_1_out));  // open: next, clr
  assign bit_extender_1_out = {{13{1'b0}}, random_1_out};  // Bit_Extender bit_extender_1
  Counter #(.width(3), .max('h5)) counter_1 (
    .Q(counter_1_q), .carry(counter_1_carry), .clk(not_1_out), .clr(not_2_out));  // open: load, D, count
  not not_1 (not_1_out, clock);
  Multiplexer #(.select(3), .width(16), .enable("false")) multiplexer_1 (
    .in0({16{1'b0}}), .in1(16'h80), .in2(16'h82), .in3(16'hac), .in4(16'h84), .out(multiplexer_1_out),
    .sel(counter_1_q));  // open: in5, in6, in7
  Multiplexer #(.select(3), .width(16), .enable("false")) multiplexer_2 (
    .in0({16{1'b0}}), .in1(x), .in2(y), .in3(bit_extender_1_out), .in4(16'h1), .out(multiplexer_2_out),
    .sel(counter_1_q));  // open: in5, in6, in7
  D_Flip_Flop activate (.clk(run), .D(run), .Q(activate_q), .reset(counter_1_carry));  // open: Qn, preset, en
  assign adr = writing ? multiplexer_1_out : 16'bz;  // Controlled_Buffer controlled_buffer_2
  // Probe on multiplexer_1_out
  assign val = writing ? multiplexer_2_out : 16'bz;  // Controlled_Buffer controlled_buffer_3
  // Probe on multiplexer_2_out
  not not_2 (not_2_out, writing);
  buf buffer_1 (write, writing);
  D_Flip_Flop #(.trigger("falling")) synchronizer (
    .clk(clock), .D(activate_q), .Q(writing), .reset(counter_1_carry));  // open: Qn, preset, en

  // Other names for the same wires on the sheet: clk = clock

  // Notes on the sheet:
  //   buffer_1 drives only 1 and floats otherwise
endmodule

module check2_writer (
  input  run,
  input  clock,
  input  clock_2,
  output [15:0] adr,
  output [15:0] val,
  output write,
  output write_2,
  output write_3
);

  wire activator_q, counter_1_carry, not_1_out, undriven, undriven_3, writing;
  wire [1:0] counter_1_q, undriven_2;
  wire [15:0] multiplexer_1_out, multiplexer_2_out;

  Register #(.width(16)) register_1 ();  // open: D, en, Q, clk, clr
  Counter #(.width(2), .max('h2)) counter_1 (
    .load(undriven), .D(undriven_2), .count(undriven_3), .Q(counter_1_q), .carry(counter_1_carry),
    .clk(clock), .clr(not_1_out));
  Counter #(.width(2), .max('h2)) counter_2 (
    .load(undriven), .D(undriven_2), .count(undriven_3), .Q(counter_1_q), .carry(counter_1_carry),
    .clk(clock), .clr(not_1_out));
  Multiplexer #(.select(2), .width(16), .enable("false")) multiplexer_1 (
    .in0({16{1'b0}}), .in1(16'h84), .out(multiplexer_1_out), .sel(counter_1_q));  // open: in2, in3
  Multiplexer #(.select(2), .width(16), .enable("false")) multiplexer_2 (
    .in0({16{1'b0}}), .in1(16'h2), .out(multiplexer_2_out), .sel(counter_1_q));  // open: in2, in3
  D_Flip_Flop activator (.clk(run), .D(run), .Q(activator_q), .reset(counter_1_carry));  // open: Qn, preset, en
  // Probe on multiplexer_1_out
  assign adr = writing ? multiplexer_1_out : 16'bz;  // Controlled_Buffer controlled_buffer_1
  assign val = writing ? multiplexer_2_out : 16'bz;  // Controlled_Buffer controlled_buffer_2
  // Probe on multiplexer_2_out
  // Probe on multiplexer_2_out
  not not_1 (not_1_out, writing);
  D_Flip_Flop #(.trigger("falling")) synchronizer (
    .clk(clock), .D(activator_q), .Q(writing), .reset(counter_1_carry));  // open: Qn, preset, en
  buf buffer_1 (write, writing);

  assign clock_2 = clock;
  assign write_2 = write;
  assign write_3 = write;

  // Other names for the same wires on the sheet: clk = clock

  // Notes on the sheet:
  //   buffer_1 drives only 1 and floats otherwise
endmodule

module shoot_writer (
  input  [15:0] x,
  input  [15:0] y,
  input  run,
  input  clock,
  output [15:0] adr,
  output [15:0] val,
  output write
);

  wire counter_1_carry, not_1_out, not_2_out, writing;
  wire [1:0] bit_extender_1_out;
  wire [2:0] counter_1_q;
  wire [15:0] multiplexer_1_out, multiplexer_2_out;

  Counter #(.width(3), .max('h5)) counter_1 (
    .Q(counter_1_q), .carry(counter_1_carry), .clk(not_1_out), .clr(not_2_out));  // open: load, D, count
  not not_1 (not_1_out, clock);
  Bit_Extender #(.in_width(3), .out_width(2)) bit_extender_1 (.in(counter_1_q), .out(bit_extender_1_out));
  Multiplexer #(.select(2), .width(16), .enable("false")) multiplexer_1 (
    .in0({16{1'b0}}), .in1(16'ha0), .in2(16'ha8), .in3(16'haa), .out(multiplexer_1_out),
    .sel(bit_extender_1_out));
  Multiplexer #(.select(2), .width(16), .enable("false")) multiplexer_2 (
    .in0({16{1'b0}}), .in1(16'h1), .in2(x), .in3(y), .out(multiplexer_2_out), .sel(bit_extender_1_out));
  // Probe on multiplexer_1_out
  assign adr = writing ? multiplexer_1_out : 16'bz;  // Controlled_Buffer controlled_buffer_1
  assign val = writing ? multiplexer_2_out : 16'bz;  // Controlled_Buffer controlled_buffer_2
  // Probe on multiplexer_2_out
  not not_2 (not_2_out, writing);
  D_Flip_Flop activator (.clk(run), .D(run), .reset(counter_1_carry));  // open: Q, Qn, preset, en
  buf buffer_1 (write, writing);
  D_Flip_Flop #(.trigger("falling")) synchronizer (.clk(clock), .reset(counter_1_carry));  // open: D, Q, Qn, preset, en

  // Other names for the same wires on the sheet: clk = clock

  // Notes on the sheet:
  //   buffer_1 drives only 1 and floats otherwise
endmodule

module collision_writer (
  input  [15:0] collided,
  input  run,
  input  clock,
  output [15:0] out_4,
  output [15:0] val,
  output write
);

  wire activator_q, counter_1_carry, not_1_out, not_2_out, writing;
  wire [1:0] counter_1_q;
  wire [15:0] multiplexer_1_out, multiplexer_2_out;

  Counter #(.width(2), .max('h2)) counter_1 (
    .Q(counter_1_q), .carry(counter_1_carry), .clk(not_1_out), .clr(not_2_out));  // open: load, D, count
  not not_1 (not_1_out, clock);
  Multiplexer #(.select(2), .width(16), .enable("false")) multiplexer_1 (
    .in0({16{1'b0}}), .in1(16'h94), .out(multiplexer_1_out), .sel(counter_1_q));  // open: in2, in3
  Multiplexer #(.select(2), .width(16), .enable("false")) multiplexer_2 (
    .in0({16{1'b0}}), .in1(collided), .out(multiplexer_2_out), .sel(counter_1_q));  // open: in2, in3
  assign out_4 = writing ? multiplexer_1_out : 16'bz;  // Controlled_Buffer controlled_buffer_1
  // Probe on multiplexer_1_out
  assign val = writing ? multiplexer_2_out : 16'bz;  // Controlled_Buffer controlled_buffer_2
  not not_2 (not_2_out, writing);
  D_Flip_Flop activator (.clk(run), .D(run), .Q(activator_q), .reset(counter_1_carry));  // open: Qn, preset, en
  buf buffer_1 (write, writing);
  D_Flip_Flop #(.trigger("falling")) synchronizer (
    .clk(clock), .D(activator_q), .Q(writing), .reset(counter_1_carry));  // open: Qn, preset, en

  // Other names for the same wires on the sheet: clk = clock

  // Notes on the sheet:
  //   buffer_1 drives only 1 and floats otherwise
endmodule

module controller (
  input  left,
  input  right,
  output [15:0] x_vec,
  output [31:0] line_x1
);

  Multiplexer #(.select(2), .width(16), .enable("false")) multiplexer_1 (
    .in0({16{1'b0}}), .in1(16'h2), .in2(16'hfffe), .in3({16{1'b0}}), .out(x_vec), .sel({left, right}));
endmodule

module bin_to_dec (
  input  [15:0] input_hex,
  input  [31:0] \input ,
  input  [4:0] y,
  output [31:0] out_4,
  output [31:0] out_5,
  output [3:0] output_2,
  output [3:0] output_1,
  output [31:0] out_8,
  output [31:0] out_9,
  output [31:0] out_10,
  output [31:0] out_11,
  output [31:0] out_12,
  output [31:0] out_13,
  output [31:0] out_14,
  output [31:0] out_15,
  output [31:0] out_16,
  output [31:0] out_17,
  output [31:0] out_18,
  output [31:0] out_19,
  output [31:0] out_20,
  output [31:0] out_21,
  output [31:0] out_22,
  output [31:0] out_23,
  output [31:0] out_24,
  output [31:0] out_25,
  output [31:0] out_26,
  output [31:0] out_27,
  output [31:0] out_28,
  output [31:0] out_29,
  output [31:0] out_30,
  output [31:0] out_31
);

  wire [15:0] divider_1_out, divider_1_rem, divider_2_rem;
  wire [31:0] r0, r2, r3, r4, r5, r6, r11, r16, r21, r22, r25, r29;

  Decoder #(.select(5), .disabled(0)) decoder_1 ();  // open: out0, out1, out2, out3, out4, out5, out6, out7, out8, out9, out10, out11, out12, out13, out14, out15, out16, out17, out18, out19, out20, out21, out22, out23, out24, out25, out26, out27, out28, out29, out30, out31, sel, en
  Divider #(.width(16)) divider_1 (.a(input_hex), .b(16'ha), .out(divider_1_out), .rem(divider_1_rem));  // open: upper
  Divider #(.width(16)) divider_2 (.a(divider_1_out), .b(16'ha), .rem(divider_2_rem));  // open: out, upper
  Bit_Extender #(.in_width(16), .out_width(4)) bit_extender_1 (.in(divider_2_rem), .out(output_2));
  Bit_Extender #(.in_width(16), .out_width(4)) bit_extender_2 (.in(divider_1_rem), .out(output_1));
  // _32buffer_el 32buffer_el_1: pin names not known; wires that end beside it: r0
  _32buffer_el u_32buffer_el_2 ();  // open: input, input_2, _1___buffer_read, _1___buffer_read_2, video, video_2, _1___buffer_write___clr
  // _32buffer_el 32buffer_el_3: pin names not known; wires that end beside it: r2
  // _32buffer_el 32buffer_el_4: pin names not known; wires that end beside it: r3
  // _32buffer_el 32buffer_el_5: pin names not known; wires that end beside it: r4
  // _32buffer_el 32buffer_el_6: pin names not known; wires that end beside it: r5
  // _32buffer_el 32buffer_el_7: pin names not known; wires that end beside it: r6
  _32buffer_el u_32buffer_el_8 ();  // open: input, input_2, _1___buffer_read, _1___buffer_read_2, video, video_2, _1___buffer_write___clr
  _32buffer_el u_32buffer_el_9 ();  // open: input, input_2, _1___buffer_read, _1___buffer_read_2, video, video_2, _1___buffer_write___clr
  // _32buffer_el 32buffer_el_10: pin names not known; wires that end beside it: r11
  _32buffer_el u_32buffer_el_11 ();  // open: input, input_2, _1___buffer_read, _1___buffer_read_2, video, video_2, _1___buffer_write___clr
  _32buffer_el u_32buffer_el_12 ();  // open: input, input_2, _1___buffer_read, _1___buffer_read_2, video, video_2, _1___buffer_write___clr
  // _32buffer_el 32buffer_el_13: pin names not known; wires that end beside it: r16
  _32buffer_el u_32buffer_el_14 ();  // open: input, input_2, _1___buffer_read, _1___buffer_read_2, video, video_2, _1___buffer_write___clr
  // _32buffer_el 32buffer_el_15: pin names not known; wires that end beside it: r21
  // _32buffer_el 32buffer_el_16: pin names not known; wires that end beside it: r22
  _32buffer_el u_32buffer_el_17 ();  // open: input, input_2, _1___buffer_read, _1___buffer_read_2, video, video_2, _1___buffer_write___clr
  // _32buffer_el 32buffer_el_18: pin names not known; wires that end beside it: r25
  _32buffer_el u_32buffer_el_19 ();  // open: input, input_2, _1___buffer_read, _1___buffer_read_2, video, video_2, _1___buffer_write___clr
  // _32buffer_el 32buffer_el_20: pin names not known; wires that end beside it: r29
endmodule

module multilayer_video_buffer_32x32 (
  input  [31:0] in_1,
  input  [31:0] in_2,
  input  [31:0] in_3,
  input  [31:0] in_4,
  input  [31:0] in_5,
  input  [31:0] in_6,
  input  write,
  input  [31:0] in_8,
  input  [31:0] \input ,
  input  [4:0] y,
  input  show,
  input  [31:0] in_12,
  input  [31:0] in_13,
  input  [31:0] in_14,
  input  [31:0] in_15,
  input  [31:0] in_16,
  input  [31:0] in_17,
  input  [31:0] in_18,
  input  [31:0] in_19,
  input  [31:0] in_20,
  input  [31:0] in_21,
  input  [31:0] in_22,
  input  [31:0] in_23,
  input  [31:0] in_24,
  input  [31:0] in_25,
  input  [31:0] in_26,
  input  [31:0] in_27,
  input  [31:0] in_28,
  input  [31:0] in_29,
  input  [31:0] in_30,
  input  [31:0] in_31,
  input  [31:0] in_32,
  input  [31:0] in_33,
  input  [31:0] in_34,
  input  [31:0] in_35,
  input  [31:0] in_36,
  output [31:0] out_37,
  output [31:0] out_38,
  output [31:0] out_39,
  output [31:0] out_40,
  output [31:0] out_41,
  output [31:0] out_42,
  output [31:0] out_43,
  output [31:0] out_44,
  output [31:0] out_45,
  output [31:0] out_46,
  output [31:0] out_47,
  output [31:0] out_48,
  output [31:0] out_49,
  output [31:0] out_50,
  output [31:0] out_51,
  output [31:0] out_52,
  output [31:0] out_53,
  output [31:0] out_54,
  output [31:0] out_55,
  output [31:0] out_56,
  output [31:0] out_57,
  output [31:0] out_58,
  output [31:0] out_59,
  output [31:0] out_60,
  output [31:0] out_61,
  output [31:0] out_62,
  output [31:0] out_63,
  output [31:0] out_64,
  output [31:0] out_65,
  output [31:0] out_66,
  output [31:0] out_67,
  output [31:0] out_68
);

  wire _0, _1, _2, _3, _4, _5, _6, _7, _8, _9, _10, _11, _12, _13, _14, _15, _16, _17, _18, _19, _20, _21,
       _22, _23, _24, _25, _26, _27, _28, _29, _30, _31;
  wire [31:0] n32buffer_el_1_p3, n32buffer_el_2_p3, n32buffer_el_3_p3, n32buffer_el_4_p3, n32buffer_el_5_p3,
       n32buffer_el_6_p3, n32buffer_el_7_p3, n32buffer_el_8_p3, n32buffer_el_9_p3, n32buffer_el_10_p3,
       n32buffer_el_11_p3, n32buffer_el_12_p3, n32buffer_el_13_p3, n32buffer_el_14_p3, n32buffer_el_15_p3,
       n32buffer_el_16_p3, n32buffer_el_17_p3, n32buffer_el_18_p3, n32buffer_el_19_p3, n32buffer_el_20_p3,
       n32buffer_el_21_p3, n32buffer_el_22_p3, n32buffer_el_23_p3, n32buffer_el_24_p3, n32buffer_el_25_p3,
       n32buffer_el_26_p3, n32buffer_el_27_p3, n32buffer_el_28_p3, n32buffer_el_29_p3, n32buffer_el_30_p3,
       n32buffer_el_31_p3, n32buffer_el_32_p3;

  Decoder #(.select(5), .disabled(0)) decoder_1 (
    .out0(_0), .out1(_1), .out2(_2), .out3(_3), .out4(_4), .out5(_5), .out6(_6), .out7(_7), .out8(_8),
    .out9(_9), .out10(_10), .out11(_11), .out12(_12), .out13(_13), .out14(_14), .out15(_15), .out16(_16),
    .out17(_17), .out18(_18), .out19(_19), .out20(_20), .out21(_21), .out22(_22), .out23(_23), .out24(_24),
    .out25(_25), .out26(_26), .out27(_27), .out28(_28), .out29(_29), .out30(_30), .out31(_31), .sel(y),
    .en(write));
  // _32buffer_el 32buffer_el_1: pin names not known; wires that end beside it: \input , _0, n32buffer_el_1_p3, show
  // _32buffer_el 32buffer_el_2: pin names not known; wires that end beside it: \input , _1, n32buffer_el_2_p3, show
  // _32buffer_el 32buffer_el_3: pin names not known; wires that end beside it: \input , _2, n32buffer_el_3_p3, show
  // _32buffer_el 32buffer_el_4: pin names not known; wires that end beside it: \input , _3, n32buffer_el_4_p3, show
  // _32buffer_el 32buffer_el_5: pin names not known; wires that end beside it: \input , _4, n32buffer_el_5_p3, show
  // _32buffer_el 32buffer_el_6: pin names not known; wires that end beside it: \input , _5, n32buffer_el_6_p3, show
  // _32buffer_el 32buffer_el_7: pin names not known; wires that end beside it: \input , _6, n32buffer_el_7_p3, show
  // _32buffer_el 32buffer_el_8: pin names not known; wires that end beside it: \input , _7, n32buffer_el_8_p3, show
  // _32buffer_el 32buffer_el_9: pin names not known; wires that end beside it: \input , _8, n32buffer_el_9_p3, show
  // _32buffer_el 32buffer_el_10: pin names not known; wires that end beside it: \input , _9, n32buffer_el_10_p3, show
  // _32buffer_el 32buffer_el_11: pin names not known; wires that end beside it: \input , _10, n32buffer_el_11_p3, show
  // _32buffer_el 32buffer_el_12: pin names not known; wires that end beside it: \input , _11, n32buffer_el_12_p3, show
  // _32buffer_el 32buffer_el_13: pin names not known; wires that end beside it: \input , _12, n32buffer_el_13_p3, show
  // _32buffer_el 32buffer_el_14: pin names not known; wires that end beside it: \input , _13, n32buffer_el_14_p3, show
  // _32buffer_el 32buffer_el_15: pin names not known; wires that end beside it: \input , _14, n32buffer_el_15_p3, show
  // _32buffer_el 32buffer_el_16: pin names not known; wires that end beside it: \input , _15, n32buffer_el_16_p3, show
  // _32buffer_el 32buffer_el_17: pin names not known; wires that end beside it: \input , _16, n32buffer_el_17_p3, show
  // _32buffer_el 32buffer_el_18: pin names not known; wires that end beside it: \input , _17, n32buffer_el_18_p3, show
  // _32buffer_el 32buffer_el_19: pin names not known; wires that end beside it: \input , _18, n32buffer_el_19_p3, show
  // _32buffer_el 32buffer_el_20: pin names not known; wires that end beside it: \input , _19, n32buffer_el_20_p3, show
  // _32buffer_el 32buffer_el_21: pin names not known; wires that end beside it: \input , _20, n32buffer_el_21_p3, show
  // _32buffer_el 32buffer_el_22: pin names not known; wires that end beside it: \input , _21, n32buffer_el_22_p3, show
  // _32buffer_el 32buffer_el_23: pin names not known; wires that end beside it: \input , _22, n32buffer_el_23_p3, show
  // _32buffer_el 32buffer_el_24: pin names not known; wires that end beside it: \input , _23, n32buffer_el_24_p3, show
  // _32buffer_el 32buffer_el_25: pin names not known; wires that end beside it: \input , _24, n32buffer_el_25_p3, show
  // _32buffer_el 32buffer_el_26: pin names not known; wires that end beside it: \input , _25, n32buffer_el_26_p3, show
  // _32buffer_el 32buffer_el_27: pin names not known; wires that end beside it: \input , _26, n32buffer_el_27_p3, show
  // _32buffer_el 32buffer_el_28: pin names not known; wires that end beside it: \input , _27, n32buffer_el_28_p3, show
  // _32buffer_el 32buffer_el_29: pin names not known; wires that end beside it: \input , _28, n32buffer_el_29_p3, show
  // _32buffer_el 32buffer_el_30: pin names not known; wires that end beside it: \input , _29, n32buffer_el_30_p3, show
  // _32buffer_el 32buffer_el_31: pin names not known; wires that end beside it: \input , _30, n32buffer_el_31_p3, show
  // _32buffer_el 32buffer_el_32: pin names not known; wires that end beside it: \input , _31, n32buffer_el_32_p3, show
  assign out_37 = in_1 | n32buffer_el_1_p3;  // OR_Gate or_1, 32 bits wide
  assign out_38 = in_2 | n32buffer_el_2_p3;  // OR_Gate or_2, 32 bits wide
  assign out_39 = in_3 | n32buffer_el_3_p3;  // OR_Gate or_3, 32 bits wide
  assign out_40 = in_4 | n32buffer_el_4_p3;  // OR_Gate or_4, 32 bits wide
  assign out_41 = in_5 | n32buffer_el_5_p3;  // OR_Gate or_5, 32 bits wide
  assign out_42 = in_6 | n32buffer_el_6_p3;  // OR_Gate or_6, 32 bits wide
  assign out_43 = in_8 | n32buffer_el_7_p3;  // OR_Gate or_7, 32 bits wide
  assign out_44 = in_12 | n32buffer_el_8_p3;  // OR_Gate or_8, 32 bits wide
  assign out_45 = in_13 | n32buffer_el_9_p3;  // OR_Gate or_9, 32 bits wide
  assign out_46 = in_14 | n32buffer_el_10_p3;  // OR_Gate or_10, 32 bits wide
  assign out_47 = in_15 | n32buffer_el_11_p3;  // OR_Gate or_11, 32 bits wide
  assign out_48 = in_16 | n32buffer_el_12_p3;  // OR_Gate or_12, 32 bits wide
  assign out_49 = in_17 | n32buffer_el_13_p3;  // OR_Gate or_13, 32 bits wide
  assign out_50 = in_18 | n32buffer_el_14_p3;  // OR_Gate or_14, 32 bits wide
  assign out_51 = in_19 | n32buffer_el_15_p3;  // OR_Gate or_15, 32 bits wide
  assign out_52 = in_20 | n32buffer_el_16_p3;  // OR_Gate or_16, 32 bits wide
  assign out_53 = in_21 | n32buffer_el_17_p3;  // OR_Gate or_17, 32 bits wide
  assign out_54 = in_22 | n32buffer_el_18_p3;  // OR_Gate or_18, 32 bits wide
  assign out_55 = in_23 | n32buffer_el_19_p3;  // OR_Gate or_19, 32 bits wide
  assign out_56 = in_24 | n32buffer_el_20_p3;  // OR_Gate or_20, 32 bits wide
  assign out_57 = in_25 | n32buffer_el_21_p3;  // OR_Gate or_21, 32 bits wide
  assign out_58 = in_26 | n32buffer_el_22_p3;  // OR_Gate or_22, 32 bits wide
  assign out_59 = in_27 | n32buffer_el_23_p3;  // OR_Gate or_23, 32 bits wide
  assign out_60 = in_28 | n32buffer_el_24_p3;  // OR_Gate or_24, 32 bits wide
  assign out_61 = in_29 | n32buffer_el_25_p3;  // OR_Gate or_25, 32 bits wide
  assign out_62 = in_30 | n32buffer_el_26_p3;  // OR_Gate or_26, 32 bits wide
  assign out_63 = in_31 | n32buffer_el_27_p3;  // OR_Gate or_27, 32 bits wide
  assign out_64 = in_32 | n32buffer_el_28_p3;  // OR_Gate or_28, 32 bits wide
  assign out_65 = in_33 | n32buffer_el_29_p3;  // OR_Gate or_29, 32 bits wide
  assign out_66 = in_34 | n32buffer_el_30_p3;  // OR_Gate or_30, 32 bits wide
  assign out_67 = in_35 | n32buffer_el_31_p3;  // OR_Gate or_31, 32 bits wide
  assign out_68 = in_36 | n32buffer_el_32_p3;  // OR_Gate or_32, 32 bits wide

  // Other names for the same wires on the sheet: inp[31:0] = \input ; w = show

  // Notes on the sheet:
  //   in_21: pull=down
  //   in_28: pull=down
  //   in_29: pull=down
  //   in_24: pull=down
  //   in_31: pull=down
  //   in_12: pull=down
  //   in_27: pull=down
  //   in_17: pull=down
  //   in_5: pull=down
  //   in_6: pull=down
  //   in_19: pull=down
  //   in_1: pull=down
  //   in_33: pull=down
  //   in_30: pull=down
  //   in_35: pull=down
  //   in_23: pull=down
  //   in_36: pull=down
  //   in_3: pull=down
  //   in_15: pull=down
  //   in_22: pull=down
  //   write: pull=down
  //   in_18: pull=down
  //   in_20: pull=down
  //   in_4: pull=down
  //   in_25: pull=down
  //   in_34: pull=down
  //   in_26: pull=down
  //   in_32: pull=down
  //   in_8: pull=down
  //   in_13: pull=down
  //   in_2: pull=down
  //   in_16: pull=down
  //   in_14: pull=down
endmodule

module priority_thread_selector (
  input  request,
  input  request_2,
  input  request_3,
  output access,
  output access_2,
  output access_3,
  output writing
);

  wire blocker_1_out_3, blocker_2_out_3, request_wait_1_out, request_wait_2_out, request_wait_3_out;

  request_wait request_wait_1 (.\wait (writing), .write(request), .out(request_wait_1_out));
  blocker blocker_1 (.out_3(blocker_1_out_3), .in_1(request_wait_1_out), .out_4(access));  // open: in_2
  buf buffer_1 (writing, access);
  Pull_Resistor pull_resistor_1 (.node(writing));
  request_wait request_wait_2 (.\wait (writing), .write(request_2), .out(request_wait_2_out));
  blocker blocker_2 (.out_3(blocker_2_out_3), .in_1(request_wait_2_out), .out_4(access_2), .in_2(blocker_1_out_3));
  buf buffer_2 (writing, access_2);
  request_wait request_wait_3 (.\wait (writing), .write(request_3), .out(request_wait_3_out));
  blocker blocker_3 (.in_1(request_wait_3_out), .out_4(access_3), .in_2(blocker_2_out_3));  // open: out_3
  buf buffer_3 (writing, access_3);

  // Notes on the sheet:
  //   buffer_1 drives only 1 and floats otherwise
  //   buffer_2 drives only 1 and floats otherwise
  //   buffer_3 drives only 1 and floats otherwise
endmodule

module request_wait (
  input  \wait ,
  input  write,
  output out
);

  wire or_1_out;

  or or_1 (or_1_out, out, ~\wait );  // OR_Gate
  D_Flip_Flop #(.trigger("high")) d_ff_1 (.clk(or_1_out), .D(write), .Q(out));  // open: Qn, preset, en, reset
endmodule

module blocker (
  input  in_1,
  input  in_2,
  output out_3,
  output out_4
);

  and and_1 (out_4, ~in_2, in_1);  // AND_Gate
  or or_1 (out_3, in_2, out_4);

  // Notes on the sheet:
  //   in_2: pull=down
endmodule

module drawer (
  input  [15:0] in_1,
  input  [4:0] in_2,
  input  [4:0] in_3,
  input  [15:0] in_4,
  input  clk,
  output out_6,
  output out_7,
  output [31:0] out_8,
  output [4:0] out_9,
  output out_10
);

  wire activator_q, and_1_out, counter_1_carry, drawing, not_1_out, pull_resistor_1_node, transistor_1_out;
  wire [4:0] counter_1_q;
  wire [15:0] adder_1_out, bit_extender_1_out, multiplier_1_out;
  wire [31:0] rom_1_data;

  simple_drawer_32x32 simple_drawer_32x32_1 (
    .x(in_2), .y(in_3), .texture_line(counter_1_q), .texture_input(rom_1_data), .cur_line(out_9),
    .line_x1(out_8));
  Counter #(.width(5), .max('h2)) counter_1 (
    .Q(counter_1_q), .carry(counter_1_carry), .clk(transistor_1_out), .clr(and_1_out));  // open: load, D, count
  Transistor #(.\type ("n"), .gate("br")) transistor_1 (.in(clk), .out(transistor_1_out), .gate(drawing));
  and and_1 (and_1_out, ~clk, counter_1_carry);  // AND_Gate
  D_Flip_Flop #(.trigger("falling")) synchronizer (
    .clk(clk), .D(activator_q), .Q(drawing), .reset(and_1_out));  // open: Qn, preset, en
  D_Flip_Flop activator (
    .clk(pull_resistor_1_node), .D(pull_resistor_1_node), .Q(activator_q), .reset(and_1_out));  // open: Qn, preset, en
  or or_1 (out_6, drawing, activator_q, and_1_out);
  assign bit_extender_1_out = {{11{1'b0}}, counter_1_q};  // Bit_Extender bit_extender_1
  Multiplier #(.width(16)) multiplier_1 (.a(in_1), .b(16'h3), .out(multiplier_1_out));  // open: cin, cout
  // Probe on in_1
  Adder #(.width(16)) adder_1 (.a(bit_extender_1_out), .b(multiplier_1_out), .out(adder_1_out));  // open: cin, cout
  Pull_Resistor pull_resistor_1 (.node(pull_resistor_1_node));
  Comparator #(.width(16), .mode("unsigned")) comparator_1 (
    .a(in_4), .b(16'h1), .eq(pull_resistor_1_node));  // open: gt, lt
  Comparator #(.width(16), .mode("unsigned")) comparator_2 (.a(in_4), .b(16'h2), .eq(out_10));  // open: gt, lt
  Pull_Resistor pull_resistor_2 (.node(out_10));
  and and_2 (out_7, drawing, not_1_out);
  not not_1 (not_1_out, clk);
  ROM #(.addrWidth(16), .dataWidth(32)) rom_1 (.addr(adder_1_out), .data(rom_1_data));  // open: sel

  // Other names for the same wires on the sheet: cmd_show = out_10

  // Notes on the sheet:
  //   texture line counter
  //   contents of rom_1 (hex, n*v repeats v):
  //   2 7 5 2 5 5 0 0 0 2 7 5 2 5 5 7 5 5 2 7 7 2 5 7 2 5 5 0 0 0 1 1 1 1151 1351 1551 1955 1155 114a
  //   7ce381 41441 3ce441 50441 51441 7ce39f 1 1 1 0 0 0 2 1 0 2 3 0 3 3
endmodule

module requester (
  input  make_request,
  input  response,
  input  writing_data,
  output permission_received,
  output request
);

  wire and_1_out, and_2_out, d_ff_1_q, d_ff_1_qn, or_1_out, register_1_q;

  D_Flip_Flop d_ff_1 (
    .clk(make_request), .D(make_request), .Q(d_ff_1_q), .Qn(d_ff_1_qn), .reset(writing_data));  // open: preset, en
  Register #(.width(1)) register_1 (.D(d_ff_1_q), .Q(register_1_q), .clk(writing_data), .clr(and_1_out));  // open: en
  and and_1 (and_1_out, d_ff_1_qn, ~writing_data);  // AND_Gate
  or or_1 (or_1_out, d_ff_1_q, and_2_out);
  and and_2 (and_2_out, register_1_q, writing_data);
  buf buffer_1 (request, or_1_out);
  and and_3 (permission_received, or_1_out, response);

  // Notes on the sheet:
  //   response: pull=down
  //   writing_data: pull=down
  //   make_request: pull=down
  //   buffer_1 drives only 1 and floats otherwise
endmodule

module bullet_thread (
  input  run,
  input  drawing,
  input  [15:0] adr,
  input  clk,
  input  [15:0] val,
  input  write,
  input  collided,
  input  end_cycle,
  output [15:0] id,
  output [4:0] x,
  output [4:0] y,
  output [15:0] command,
  output collide_check_player,
  output collide_check_enemy,
  output collide_check_wall,
  output [15:0] x_col,
  output [15:0] y_col
);

  wire and_1_out, and_2_out, and_6_out, and_7_out, and_8_out, and_9_out, and_10_out, and_11_out, and_12_out,
       and_13_out, bot, bullet_object_1_avaiable, bullet_object_1_ready, bullet_object_2_avaiable,
       bullet_object_2_ready, bullet_object_3_avaiable, bullet_object_3_ready, bullet_object_4_avaiable,
       bullet_object_4_ready, command_draw, comparator_1_eq, comparator_2_eq, comparator_6_eq,
       comparator_9_eq, counter_1_carry, cycle, d_ff_1_qn, d_ff_2_qn, enemy, enemy1, enemy2, or_1_out,
       or_2_out, player, pull_resistor_4_node, pull_resistor_5_node, pull_resistor_6_node,
       pull_resistor_9_node, runnable, xor_1_out;
  wire [15:0] bullet_object_1_x, bullet_object_1_y, button_q, divider_1_out, divider_2_out, enemy_spawn_x,
       enemy_spawn_y, player_spawn_x, player_spawn_y, rand_q, shifter_1_out, shifter_2_out, spawn_x, spawn_y;

  and and_1 (and_1_out, run, runnable);
  D_Flip_Flop d_ff_1 (.clk(cycle), .D(cycle), .Qn(d_ff_1_qn), .reset(counter_1_carry));  // open: Q, preset, en
  or or_1 (or_1_out, bot, player, enemy);
  Counter #(.width(2), .max('h3)) counter_1 (
    .carry(counter_1_carry), .clk(clk), .clr(d_ff_1_qn));  // open: load, D, count, Q
  and and_2 (and_2_out, runnable, or_1_out);
  xor xor_1 (xor_1_out, counter_1_carry, and_1_out);
  bullet_object bullet_object_1 (
    .draw(xor_1_out), .spawn_id(16'hf), .spawn_x(enemy_spawn_x), .spawn_y(enemy_spawn_y), .y_vec(16'h2),
    .ready(bullet_object_1_ready), .id(id), .x(bullet_object_1_x), .y(bullet_object_1_y), .command(command),
    .avaiable(bullet_object_1_avaiable), .clk(clk), .end_cycle(end_cycle), .delete(collided), .spawn(enemy1),
    .\wait (drawing));
  and and_3 (enemy1, bullet_object_1_avaiable, enemy);
  bullet_object bullet_object_2 (
    .draw(bullet_object_1_ready), .spawn_id(16'hf), .spawn_x(enemy_spawn_x), .spawn_y(enemy_spawn_y),
    .y_vec(16'h2), .ready(bullet_object_2_ready), .id(id), .x(bullet_object_1_x), .y(bullet_object_1_y),
    .command(command), .avaiable(bullet_object_2_avaiable), .clk(clk), .end_cycle(end_cycle),
    .delete(collided), .spawn(enemy2), .\wait (drawing));
  and and_4 (runnable, bullet_object_1_avaiable, bullet_object_2_avaiable, bullet_object_3_avaiable, bullet_object_4_avaiable);
  and and_5 (enemy2, ~bullet_object_1_avaiable, bullet_object_2_avaiable, enemy);  // AND_Gate
  bullet_object bullet_object_3 (
    .draw(bullet_object_2_ready), .spawn_id(16'ha), .spawn_x(player_spawn_x), .spawn_y(player_spawn_y),
    .y_vec(16'hfffe), .ready(bullet_object_3_ready), .id(id), .x(bullet_object_1_x), .y(bullet_object_1_y),
    .command(command), .avaiable(bullet_object_3_avaiable), .clk(clk), .end_cycle(end_cycle),
    .delete(collided), .spawn(player), .\wait (drawing));
  Pull_Resistor pull_resistor_1 (.node(bot));
  bullet_object bullet_object_4 (
    .draw(bullet_object_3_ready), .spawn_id(16'ha), .spawn_x(spawn_x), .spawn_y(spawn_y), .y_vec(16'hfffe),
    .ready(bullet_object_4_ready), .id(id), .x(bullet_object_1_x), .y(bullet_object_1_y), .command(command),
    .avaiable(bullet_object_4_avaiable), .clk(clk), .end_cycle(end_cycle), .delete(collided), .spawn(bot),
    .\wait (drawing));
  Counter #(.width(2), .max('h3)) counter_2 (.carry(cycle), .clk(clk), .clr(d_ff_2_qn));  // open: load, D, count, Q
  D_Flip_Flop d_ff_2 (
    .clk(bullet_object_4_ready), .D(bullet_object_4_ready), .Qn(d_ff_2_qn), .reset(cycle));  // open: Q, preset, en
  and and_6 (and_6_out, comparator_1_eq, clk, write);
  Comparator #(.width(16), .mode("unsigned")) comparator_1 (.a(adr), .b(16'h80), .eq(comparator_1_eq));  // open: gt, lt
  Pull_Resistor pull_resistor_2 (.node(comparator_1_eq));
  and and_7 (and_7_out, comparator_2_eq, clk, write);
  Comparator #(.width(16), .mode("unsigned")) comparator_2 (.a(adr), .b(16'h82), .eq(comparator_2_eq));  // open: gt, lt
  Pull_Resistor pull_resistor_3 (.node(comparator_2_eq));
  and and_8 (and_8_out, pull_resistor_4_node, clk, write);
  Pull_Resistor pull_resistor_4 (.node(pull_resistor_4_node));
  Comparator #(.width(16), .mode("unsigned")) comparator_3 (
    .a(adr), .b(16'hac), .eq(pull_resistor_4_node));  // open: gt, lt
  and and_9 (and_9_out, pull_resistor_5_node, clk, write);
  Pull_Resistor pull_resistor_5 (.node(pull_resistor_5_node));
  Comparator #(.width(16), .mode("unsigned")) comparator_4 (
    .a(adr), .b(16'ha8), .eq(pull_resistor_5_node));  // open: gt, lt
  and and_10 (and_10_out, pull_resistor_6_node, clk, write);
  Pull_Resistor pull_resistor_6 (.node(pull_resistor_6_node));
  Comparator #(.width(16), .mode("unsigned")) comparator_5 (
    .a(adr), .b(16'haa), .eq(pull_resistor_6_node));  // open: gt, lt
  and and_11 (and_11_out, comparator_6_eq, clk, write);
  Comparator #(.width(16), .mode("unsigned")) comparator_6 (.a(adr), .b(16'ha0), .eq(comparator_6_eq));  // open: gt, lt
  Pull_Resistor pull_resistor_7 (.node(comparator_6_eq));
  Transistor #(.width(16)) transistor_1 (.in(16'h2), .out(command), .gate(d_ff_2_qn));
  Register #(.width(16)) enemy_x (.D(val), .Q(enemy_spawn_x), .clk(and_6_out));  // open: en, clr
  Register #(.width(16)) enemy_y (.D(val), .Q(enemy_spawn_y), .clk(and_7_out));  // open: en, clr
  Register #(.width(16)) \rand  (.D(val), .Q(rand_q), .clk(and_8_out), .clr(enemy));  // open: en
  Register #(.width(16)) player_x (.D(val), .Q(player_spawn_x), .clk(and_9_out));  // open: en, clr
  Register #(.width(16)) player_y (.D(val), .Q(player_spawn_y), .clk(and_10_out));  // open: en, clr
  Register #(.width(16)) button (.D(val), .Q(button_q), .clk(and_11_out), .clr(player));  // open: en
  Divider #(.width(16)) divider_1 (.a(bullet_object_1_x), .b(16'h2), .out(divider_1_out));  // open: upper, rem
  Comparator #(.width(16), .mode("unsigned")) comparator_7 (.a(rand_q), .b(16'h3), .eq(enemy));  // open: gt, lt
  Comparator #(.width(16), .mode("unsigned")) comparator_8 (.a(button_q), .b(16'h1), .eq(player));  // open: gt, lt
  Shifter #(.width(16), .shift("lr")) shifter_1 (.in(bullet_object_1_x), .\dist (4'b0001), .out(shifter_1_out));
  Bit_Extender #(.in_width(16), .out_width(5)) bit_extender_1 (.in(shifter_1_out), .out(x));
  Register #(.width(16)) u_x (.D(divider_1_out), .Q(x_col), .clk(or_2_out));  // open: en, clr
  Shifter #(.width(16), .shift("lr")) shifter_2 (.in(bullet_object_1_y), .\dist (4'b0001), .out(shifter_2_out));
  Register #(.width(16)) u_y (.D(divider_2_out), .Q(y_col), .clk(or_2_out));  // open: en, clr
  Divider #(.width(16)) divider_2 (.a(bullet_object_1_y), .b(16'h2), .out(divider_2_out));  // open: upper, rem
  Bit_Extender #(.in_width(16), .out_width(5)) bit_extender_2 (.in(shifter_2_out), .out(y));
  Comparator #(.width(16), .mode("unsigned")) comparator_9 (.a(id), .b(16'hf), .eq(comparator_9_eq));  // open: gt, lt
  Pull_Resistor pull_resistor_8 (.node(comparator_9_eq));
  Pull_Resistor pull_resistor_9 (.node(pull_resistor_9_node));
  Comparator #(.width(16), .mode("unsigned")) comparator_10 (
    .a(id), .b(16'ha), .eq(pull_resistor_9_node));  // open: gt, lt
  Pull_Resistor pull_resistor_10 (.node(command_draw));
  Comparator #(.width(16), .mode("unsigned")) comparator_11 (
    .a(command), .b(16'h1), .eq(command_draw));  // open: gt, lt
  and and_12 (and_12_out, command_draw, comparator_9_eq);
  and and_13 (and_13_out, command_draw, pull_resistor_9_node);
  or or_2 (or_2_out, and_13_out, and_12_out);
  D_Flip_Flop d_ff_3 (.clk(clk), .D(and_12_out), .Q(collide_check_player));  // open: Qn, preset, en, reset
  D_Flip_Flop d_ff_4 (.clk(clk), .D(and_13_out), .Q(collide_check_enemy));  // open: Qn, preset, en, reset
  D_Flip_Flop d_ff_5 (.clk(clk), .D(or_2_out), .Q(collide_check_wall));  // open: Qn, preset, en, reset

  // Other names for the same wires on the sheet: wait = drawing

  // Notes on the sheet:
  //   collided: pull=down
  //   Enemy bullets
  //   Allied bullets
endmodule

module bullet_object (
  input  end_cycle,
  input  draw,
  input  [15:0] spawn_id,
  input  [15:0] spawn_x,
  input  [15:0] spawn_y,
  input  delete,
  input  [15:0] y_vec,
  input  spawn,
  input  clk,
  input  \wait ,
  output avaiable,
  output ready,
  output [15:0] id,
  output [15:0] x,
  output [15:0] y,
  output [15:0] command
);

  wire activator_q, and_2_out, and_3_out, and_4_out, comparator_2_gt, comparator_3_lt, counter_1_carry,
       delete_t, draw_t, \end , or_1_out, pull_resistor_2_node, skip, update;
  wire [1:0] counter_1_q;
  wire [15:0] adder_1_out, adder_2_out, bit_extender_1_out, id_q, multiplexer_1_out, multiplexer_2_out,
       multiplexer_3_out, x_q, y_q;

  and and_1 (skip, avaiable, draw);
  D_Flip_Flop activator (.clk(draw), .D(draw), .Q(activator_q), .reset(or_1_out));  // open: Qn, preset, en
  Pull_Resistor pull_resistor_1 (.node(spawn_id));
  D_Flip_Flop #(.trigger("falling")) synchronizer (
    .clk(clk), .D(activator_q), .Q(draw_t), .reset(or_1_out));  // open: Qn, preset, en
  or or_1 (or_1_out, end_cycle, ready);
  Adder #(.width(16)) adder_1 (.a(y_q), .b(y_vec), .out(adder_1_out));  // open: cin, cout
  Multiplexer #(.width(16), .enable("false")) multiplexer_1 (
    .in0(id_q), .in1(spawn_id), .out(multiplexer_1_out), .sel(avaiable));
  Multiplexer #(.width(16), .enable("false")) multiplexer_2 (
    .in0(x_q), .in1(spawn_x), .out(multiplexer_2_out), .sel(avaiable));
  Multiplexer #(.width(16), .enable("false")) multiplexer_3 (
    .in0(adder_1_out), .in1(spawn_y), .out(multiplexer_3_out), .sel(avaiable));
  Counter #(.width(2), .max('h2)) counter_1 (
    .Q(counter_1_q), .carry(counter_1_carry), .clk(pull_resistor_2_node), .clr(counter_1_carry));  // open: load, D, count
  Pull_Resistor pull_resistor_2 (.node(pull_resistor_2_node));
  assign pull_resistor_2_node = and_2_out ? clk : 1'bz;  // Controlled_Buffer controlled_buffer_1
  and and_2 (and_2_out, draw_t, ~\wait );  // AND_Gate
  Comparator #(.width(16), .mode("unsigned")) comparator_1 (.a({16{1'b0}}), .b(id_q), .eq(avaiable));  // open: gt, lt
  Register #(.width(16)) u_id (.D(multiplexer_1_out), .Q(id_q), .clk(update), .clr(delete_t));  // open: en
  Register #(.width(16)) u_x (.D(multiplexer_2_out), .Q(x_q), .clk(update), .clr(delete_t));  // open: en
  Register #(.width(16)) u_y (.D(multiplexer_3_out), .Q(y_q), .clk(update), .clr(delete_t));  // open: en
  assign bit_extender_1_out = {{15{1'b0}}, counter_1_q[0]};  // Bit_Extender bit_extender_1
  timer timer_1 (.run(counter_1_carry), .out(\end ), .clk_2(clk), .clk(16'h4));
  assign id = draw_t ? id_q : 16'bz;  // Controlled_Buffer controlled_buffer_2
  Adder #(.width(16)) adder_2 (.a(x_q), .b(16'h2), .out(adder_2_out));  // open: cin, cout
  assign y = draw_t ? y_q : 16'bz;  // Controlled_Buffer controlled_buffer_3
  assign command = draw_t ? bit_extender_1_out : 16'bz;  // Controlled_Buffer controlled_buffer_4
  assign x = draw_t ? adder_2_out : 16'bz;  // Controlled_Buffer controlled_buffer_5
  and and_3 (and_3_out, avaiable, draw_t);
  or or_2 (update, spawn, draw_t);
  or or_3 (ready, \end , and_3_out, skip, delete_t);
  Comparator #(.width(16), .mode("unsigned")) comparator_2 (.a(y_q), .b(16'h3b), .gt(comparator_2_gt));  // open: eq, lt
  Comparator #(.width(16), .mode("unsigned")) comparator_3 (
    .a(y_q), .b({16{1'b0}}), .lt(comparator_3_lt));  // open: gt, eq
  and and_4 (and_4_out, delete, draw_t);
  or or_4 (delete_t, comparator_2_gt, comparator_3_lt, and_4_out);

  // Notes on the sheet:
  //   spawn: pull=down
  //   end_cycle: pull=down
endmodule

module timer (
  input  run,
  input  [15:0] clk,
  input  clk_2,
  output out
);

  wire d_ff_1_qn;
  wire [15:0] counter_1_q;

  D_Flip_Flop d_ff_1 (.clk(run), .D(run), .Qn(d_ff_1_qn), .reset(out));  // open: Q, preset, en
  Counter #(.width(16), .max('hffff)) counter_1 (
    .Q(counter_1_q), .clk(clk_2), .clr(d_ff_1_qn));  // open: load, D, count, carry
  Comparator #(.width(16), .mode("unsigned")) comparator_1 (.a(counter_1_q), .b(clk), .eq(out));  // open: gt, lt

  // Other names for the same wires on the sheet: clk_t = clk_2
endmodule
